// Logisim project Relógio.circ as structural Verilog: 3 circuits, main circuit main
module main (
);

  wire _0_a_1_Hora, _0_a_3_Hora, _0_a_5, _0_a_5_Min, _0_a_9, _0_a_9_Hora, _0_a_9_Min, _24_Horas, Bit1_2_H,
       Bit1_2_Min, Bit1_2_Sec, Bit2_2_H, Bit2_2_Min, Bit2_2_Sec, Bit3_2_H, Bit3_2_Min, Bit3_2_Sec, Bit4_2_H,
       Bit4_2_Min, Bit4_2_Sec, Bit_1_H, Bit_1_Min, Bit_1_Sec, Bit_2_H, Bit_2_Min, Bit_2_Sec, Bit_3_H,
       Bit_3_Min, Bit_3_Sec, Bit_4_H, Bit_4_Min, Bit_4_Sec, clock_1_out, display_7_seg_1_a,
       display_7_seg_1_b, display_7_seg_1_c, display_7_seg_1_d, display_7_seg_1_e, display_7_seg_1_f,
       display_7_seg_1_g, display_7_seg_2_a, display_7_seg_2_b, display_7_seg_2_c, display_7_seg_2_d,
       display_7_seg_2_e, display_7_seg_2_f, display_7_seg_2_g, display_7_seg_3_a, display_7_seg_3_b,
       display_7_seg_3_c, display_7_seg_3_d, display_7_seg_3_e, display_7_seg_3_f, display_7_seg_3_g,
       display_7_seg_4_a, display_7_seg_4_b, display_7_seg_4_c, display_7_seg_4_d, display_7_seg_4_e,
       display_7_seg_4_f, display_7_seg_4_g, display_7_seg_5_a, display_7_seg_5_b, display_7_seg_5_c,
       display_7_seg_5_d, display_7_seg_5_e, display_7_seg_5_f, display_7_seg_5_g, display_7_seg_6_a,
       display_7_seg_6_b, display_7_seg_6_c, display_7_seg_6_d, display_7_seg_6_e, display_7_seg_6_f,
       display_7_seg_6_g, or_1_out;

  and and_1 (_0_a_5, ~Bit4_2_Sec, Bit3_2_Sec, Bit2_2_Sec, ~Bit1_2_Sec);  // AND_Gate
  and and_2 (_0_a_5_Min, ~Bit4_2_Min, Bit3_2_Min, Bit2_2_Min, ~Bit1_2_Min);  // AND_Gate
  and and_3 (_0_a_1_Hora, ~Bit4_2_H, ~Bit3_2_H, Bit2_2_H, ~Bit1_2_H);  // AND_Gate
  Hex_Digit_Display hex_digit_display_1 (.value({Bit4_2_H, Bit3_2_H, Bit2_2_H, Bit1_2_H}));  // open: dp
  T_Flip_Flop #(.trigger("falling")) t_ff_1 (
    .clk(_0_a_9), .T(1'b1), .Q(Bit1_2_Sec), .reset(_0_a_5));  // open: Qn, preset, en
  T_Flip_Flop #(.trigger("falling")) t_ff_2 (
    .clk(_0_a_9_Min), .T(1'b1), .Q(Bit1_2_Min), .reset(_0_a_5_Min));  // open: Qn, preset, en
  T_Flip_Flop #(.trigger("falling")) t_ff_3 (
    .clk(_0_a_9_Hora), .T(1'b1), .Q(Bit1_2_H), .reset(_24_Horas));  // open: Qn, preset, en
  Hex_Digit_Display hex_digit_display_2 (.value({Bit4_2_Min, Bit3_2_Min, Bit2_2_Min, Bit1_2_Min}));  // open: dp
  Hex_Digit_Display hex_digit_display_3 (.value({Bit_4_H, Bit_3_H, Bit_2_H, Bit_1_H}));  // open: dp
  T_Flip_Flop #(.trigger("falling")) t_ff_4 (
    .clk(Bit1_2_Min), .T(1'b1), .Q(Bit2_2_Min), .reset(_0_a_5_Min));  // open: Qn, preset, en
  Hex_Digit_Display hex_digit_display_4 (.value({Bit_4_Min, Bit_3_Min, Bit_2_Min, Bit_1_Min}));  // open: dp
  Hex_Digit_Display hex_digit_display_5 (.value({Bit4_2_Sec, Bit3_2_Sec, Bit2_2_Sec, Bit1_2_Sec}));  // open: dp
  T_Flip_Flop #(.trigger("falling")) t_ff_5 (
    .clk(Bit1_2_Sec), .T(1'b1), .Q(Bit2_2_Sec), .reset(_0_a_5));  // open: Qn, preset, en
  T_Flip_Flop #(.trigger("falling")) t_ff_6 (
    .clk(Bit1_2_H), .T(1'b1), .Q(Bit2_2_H), .reset(_24_Horas));  // open: Qn, preset, en
  Hex_Digit_Display hex_digit_display_6 (.value({Bit_4_Sec, Bit_3_Sec, Bit_2_Sec, Bit_1_Sec}));  // open: dp
  T_Flip_Flop #(.trigger("falling")) t_ff_7 (
    .clk(Bit2_2_Sec), .T(1'b1), .Q(Bit3_2_Sec), .reset(_0_a_5));  // open: Qn, preset, en
  T_Flip_Flop #(.trigger("falling")) t_ff_8 (
    .clk(Bit2_2_Min), .T(1'b1), .Q(Bit3_2_Min), .reset(_0_a_5_Min));  // open: Qn, preset, en
  T_Flip_Flop #(.trigger("falling")) t_ff_9 (
    .clk(Bit2_2_H), .T(1'b1), .Q(Bit3_2_H), .reset(_24_Horas));  // open: Qn, preset, en
  and and_4 (_24_Horas, _0_a_1_Hora, _0_a_3_Hora);
  T_Flip_Flop #(.trigger("falling")) t_ff_10 (
    .clk(Bit3_2_Sec), .T(1'b1), .Q(Bit4_2_Sec), .reset(_0_a_5));  // open: Qn, preset, en
  T_Flip_Flop #(.trigger("falling")) t_ff_11 (
    .clk(Bit3_2_Min), .T(1'b1), .Q(Bit4_2_Min), .reset(_0_a_5_Min));  // open: Qn, preset, en
  T_Flip_Flop #(.trigger("falling")) t_ff_12 (
    .clk(Bit3_2_H), .T(1'b1), .Q(Bit4_2_H), .reset(_24_Horas));  // open: Qn, preset, en
  _7_Segment_Display u_7_segment_display_1 (
    .g(display_7_seg_2_g), .f(display_7_seg_2_f), .a(display_7_seg_2_a), .b(display_7_seg_2_b),
    .e(display_7_seg_2_e), .d(display_7_seg_2_d), .c(display_7_seg_2_c));  // open: dp
  _7_Segment_Display u_7_segment_display_2 (
    .g(display_7_seg_1_g), .f(display_7_seg_1_f), .a(display_7_seg_1_a), .b(display_7_seg_1_b),
    .e(display_7_seg_1_e), .d(display_7_seg_1_d), .c(display_7_seg_1_c));  // open: dp
  Display_7_Seg display_7_seg_1 (
    .a(display_7_seg_1_a), .b(display_7_seg_1_b), .c(display_7_seg_1_c), .d(display_7_seg_1_d),
    .e(display_7_seg_1_e), .f(display_7_seg_1_f), .g(display_7_seg_1_g),
    .ABCD({Bit_4_H, Bit_3_H, Bit_2_H, Bit_1_H}));
  Display_7_Seg display_7_seg_2 (
    .a(display_7_seg_2_a), .b(display_7_seg_2_b), .c(display_7_seg_2_c), .d(display_7_seg_2_d),
    .e(display_7_seg_2_e), .f(display_7_seg_2_f), .g(display_7_seg_2_g),
    .ABCD({Bit4_2_H, Bit3_2_H, Bit2_2_H, Bit1_2_H}));
  Clock clock_1 (.out(clock_1_out));
  _7_Segment_Display u_7_segment_display_3 (
    .g(display_7_seg_3_g), .f(display_7_seg_3_f), .a(display_7_seg_3_a), .b(display_7_seg_3_b),
    .e(display_7_seg_3_e), .d(display_7_seg_3_d), .c(display_7_seg_3_c));  // open: dp
  _7_Segment_Display u_7_segment_display_4 (
    .g(display_7_seg_4_g), .f(display_7_seg_4_f), .a(display_7_seg_4_a), .b(display_7_seg_4_b),
    .e(display_7_seg_4_e), .d(display_7_seg_4_d), .c(display_7_seg_4_c));  // open: dp
  Display_7_Seg display_7_seg_3 (
    .a(display_7_seg_3_a), .b(display_7_seg_3_b), .c(display_7_seg_3_c), .d(display_7_seg_3_d),
    .e(display_7_seg_3_e), .f(display_7_seg_3_f), .g(display_7_seg_3_g),
    .ABCD({Bit4_2_Min, Bit3_2_Min, Bit2_2_Min, Bit1_2_Min}));
  and and_5 (_0_a_9, Bit_4_Sec, ~Bit_3_Sec, Bit_2_Sec, ~Bit_1_Sec);  // AND_Gate
  and and_6 (_0_a_9_Min, Bit_4_Min, ~Bit_3_Min, Bit_2_Min, ~Bit_1_Min);  // AND_Gate
  or or_1 (or_1_out, _0_a_9_Hora, _24_Horas);
  and and_7 (_0_a_9_Hora, Bit_4_H, ~Bit_3_H, Bit_2_H, ~Bit_1_H);  // AND_Gate
  and and_8 (_0_a_3_Hora, ~Bit_4_H, Bit_3_H, ~Bit_2_H, ~Bit_1_H);  // AND_Gate
  _7_Segment_Display u_7_segment_display_5 (
    .g(display_7_seg_6_g), .f(display_7_seg_6_f), .a(display_7_seg_6_a), .b(display_7_seg_6_b),
    .e(display_7_seg_6_e), .d(display_7_seg_6_d), .c(display_7_seg_6_c));  // open: dp
  _7_Segment_Display u_7_segment_display_6 (
    .g(display_7_seg_5_g), .f(display_7_seg_5_f), .a(display_7_seg_5_a), .b(display_7_seg_5_b),
    .e(display_7_seg_5_e), .d(display_7_seg_5_d), .c(display_7_seg_5_c));  // open: dp
  Display_7_Seg display_7_seg_4 (
    .a(display_7_seg_4_a), .b(display_7_seg_4_b), .c(display_7_seg_4_c), .d(display_7_seg_4_d),
    .e(display_7_seg_4_e), .f(display_7_seg_4_f), .g(display_7_seg_4_g),
    .ABCD({Bit_4_Min, Bit_3_Min, Bit_2_Min, Bit_1_Min}));
  Display_7_Seg display_7_seg_5 (
    .a(display_7_seg_5_a), .b(display_7_seg_5_b), .c(display_7_seg_5_c), .d(display_7_seg_5_d),
    .e(display_7_seg_5_e), .f(display_7_seg_5_f), .g(display_7_seg_5_g),
    .ABCD({Bit4_2_Sec, Bit3_2_Sec, Bit2_2_Sec, Bit1_2_Sec}));
  T_Flip_Flop #(.trigger("falling")) t_ff_13 (
    .clk(clock_1_out), .T(1'b1), .Q(Bit_1_Sec), .reset(_0_a_9));  // open: Qn, preset, en
  T_Flip_Flop #(.trigger("falling")) t_ff_14 (
    .clk(_0_a_5), .T(1'b1), .Q(Bit_1_Min), .reset(_0_a_9_Min));  // open: Qn, preset, en
  T_Flip_Flop #(.trigger("falling")) t_ff_15 (
    .clk(_0_a_5_Min), .T(1'b1), .Q(Bit_1_H), .reset(or_1_out));  // open: Qn, preset, en
  Display_7_Seg display_7_seg_6 (
    .a(display_7_seg_6_a), .b(display_7_seg_6_b), .c(display_7_seg_6_c), .d(display_7_seg_6_d),
    .e(display_7_seg_6_e), .f(display_7_seg_6_f), .g(display_7_seg_6_g),
    .ABCD({Bit_4_Sec, Bit_3_Sec, Bit_2_Sec, Bit_1_Sec}));
  T_Flip_Flop #(.trigger("falling")) t_ff_16 (
    .clk(Bit_1_Sec), .T(1'b1), .Q(Bit_2_Sec), .reset(_0_a_9));  // open: Qn, preset, en
  T_Flip_Flop #(.trigger("falling")) t_ff_17 (
    .clk(Bit_1_Min), .T(1'b1), .Q(Bit_2_Min), .reset(_0_a_9_Min));  // open: Qn, preset, en
  T_Flip_Flop #(.trigger("falling")) t_ff_18 (
    .clk(Bit_1_H), .T(1'b1), .Q(Bit_2_H), .reset(or_1_out));  // open: Qn, preset, en
  T_Flip_Flop #(.trigger("falling")) t_ff_19 (
    .clk(Bit_2_Sec), .T(1'b1), .Q(Bit_3_Sec), .reset(_0_a_9));  // open: Qn, preset, en
  T_Flip_Flop #(.trigger("falling")) t_ff_20 (
    .clk(Bit_2_Min), .T(1'b1), .Q(Bit_3_Min), .reset(_0_a_9_Min));  // open: Qn, preset, en
  T_Flip_Flop #(.trigger("falling")) t_ff_21 (
    .clk(Bit_2_H), .T(1'b1), .Q(Bit_3_H), .reset(or_1_out));  // open: Qn, preset, en
  T_Flip_Flop #(.trigger("falling")) t_ff_22 (
    .clk(Bit_3_Sec), .T(1'b1), .Q(Bit_4_Sec), .reset(_0_a_9));  // open: Qn, preset, en
  T_Flip_Flop #(.trigger("falling")) t_ff_23 (
    .clk(Bit_3_Min), .T(1'b1), .Q(Bit_4_Min), .reset(_0_a_9_Min));  // open: Qn, preset, en
  T_Flip_Flop #(.trigger("falling")) t_ff_24 (
    .clk(Bit_3_H), .T(1'b1), .Q(Bit_4_H), .reset(or_1_out));  // open: Qn, preset, en

  // Other names for the same wires on the sheet: Horas_0_a_2[3:0] = {Bit4_2_H, Bit3_2_H, Bit2_2_H, Bit1_2_H};
  //   Horas_0_a_9[3:0] = {Bit_4_H, Bit_3_H, Bit_2_H, Bit_1_H};
  //   Minutos_0_a_5[3:0] = {Bit4_2_Min, Bit3_2_Min, Bit2_2_Min, Bit1_2_Min};
  //   Minutos_0_a_9[3:0] = {Bit_4_Min, Bit_3_Min, Bit_2_Min, Bit_1_Min};
  //   Segundos_0_a_5[3:0] = {Bit4_2_Sec, Bit3_2_Sec, Bit2_2_Sec, Bit1_2_Sec};
  //   Segundos_0_a_9[3:0] = {Bit_4_Sec, Bit_3_Sec, Bit_2_Sec, Bit_1_Sec}
endmodule

module Display_7_Seg (
  input  [3:0] ABCD,
  output a,
  output b,
  output c,
  output d,
  output e,
  output f,
  output g
);

  wire and_1_out, and_2_out, and_3_out, and_4_out, and_5_out, and_6_out, and_7_out, and_8_out, and_9_out,
       and_10_out, and_11_out, and_12_out, and_13_out, and_14_out, and_15_out, and_16_out, and_17_out,
       and_18_out, and_19_out, and_20_out, and_21_out, and_22_out, and_23_out, and_24_out, and_25_out,
       not_1_out, not_2_out, not_3_out, not_4_out, not_5_out, not_6_out, not_7_out, not_8_out, not_9_out,
       not_10_out, not_11_out, not_12_out, not_13_out, not_14_out, not_15_out, not_16_out, not_17_out,
       not_18_out, not_19_out, not_20_out, not_21_out, not_22_out, not_23_out, not_24_out, not_25_out,
       not_26_out, not_27_out, not_28_out, not_29_out, not_30_out, not_31_out, not_32_out, not_33_out,
       not_34_out, not_35_out, not_36_out, not_37_out, not_38_out, not_39_out, not_40_out, not_41_out,
       not_42_out, not_43_out, not_44_out, not_45_out, not_46_out, not_47_out;

  not not_1 (not_1_out, ABCD[3]);
  not not_2 (not_2_out, ABCD[2]);
  not not_3 (not_3_out, ABCD[0]);
  not not_4 (not_4_out, ABCD[3]);
  not not_5 (not_5_out, ABCD[3]);
  not not_6 (not_6_out, ABCD[2]);
  not not_7 (not_7_out, ABCD[1]);
  not not_8 (not_8_out, ABCD[3]);
  not not_9 (not_9_out, ABCD[2]);
  not not_10 (not_10_out, ABCD[3]);
  not not_11 (not_11_out, ABCD[1]);
  not not_12 (not_12_out, ABCD[0]);
  not not_13 (not_13_out, ABCD[2]);
  not not_14 (not_14_out, ABCD[1]);
  not not_15 (not_15_out, ABCD[3]);
  not not_16 (not_16_out, ABCD[2]);
  not not_17 (not_17_out, ABCD[1]);
  not not_18 (not_18_out, ABCD[3]);
  not not_19 (not_19_out, ABCD[3]);
  not not_20 (not_20_out, ABCD[3]);
  not not_21 (not_21_out, ABCD[2]);
  not not_22 (not_22_out, ABCD[0]);
  not not_23 (not_23_out, ABCD[3]);
  not not_24 (not_24_out, ABCD[2]);
  not not_25 (not_25_out, ABCD[3]);
  not not_26 (not_26_out, ABCD[0]);
  not not_27 (not_27_out, ABCD[3]);
  not not_28 (not_28_out, ABCD[1]);
  not not_29 (not_29_out, ABCD[2]);
  not not_30 (not_30_out, ABCD[1]);
  not not_31 (not_31_out, ABCD[2]);
  not not_32 (not_32_out, ABCD[1]);
  not not_33 (not_33_out, ABCD[0]);
  not not_34 (not_34_out, ABCD[3]);
  not not_35 (not_35_out, ABCD[0]);
  not not_36 (not_36_out, ABCD[3]);
  not not_37 (not_37_out, ABCD[1]);
  not not_38 (not_38_out, ABCD[0]);
  not not_39 (not_39_out, ABCD[3]);
  not not_40 (not_40_out, ABCD[1]);
  not not_41 (not_41_out, ABCD[3]);
  not not_42 (not_42_out, ABCD[0]);
  not not_43 (not_43_out, ABCD[2]);
  not not_44 (not_44_out, ABCD[1]);
  not not_45 (not_45_out, ABCD[2]);
  not not_46 (not_46_out, ABCD[1]);
  not not_47 (not_47_out, ABCD[0]);
  and and_1 (and_1_out, not_1_out, not_2_out, not_3_out);
  and and_2 (and_2_out, not_4_out, ABCD[1]);
  and and_3 (and_3_out, not_5_out, ABCD[2], ABCD[0]);
  and and_4 (and_4_out, ABCD[3], not_6_out, not_7_out);
  and and_5 (and_5_out, not_8_out, not_9_out);
  and and_6 (and_6_out, not_10_out, not_11_out, not_12_out);
  and and_7 (and_7_out, not_13_out, not_14_out);
  and and_8 (and_8_out, not_15_out, ABCD[1], ABCD[0]);
  and and_9 (and_9_out, not_16_out, not_17_out);
  and and_10 (and_10_out, not_18_out, ABCD[0]);
  and and_11 (and_11_out, not_19_out, ABCD[2]);
  and and_12 (and_12_out, not_20_out, not_21_out, not_22_out);
  and and_13 (and_13_out, not_23_out, not_24_out, ABCD[1]);
  and and_14 (and_14_out, not_25_out, ABCD[1], not_26_out);
  and and_15 (and_15_out, not_27_out, ABCD[2], not_28_out, ABCD[0]);
  and and_16 (and_16_out, ABCD[3], not_29_out, not_30_out);
  and and_17 (and_17_out, not_31_out, not_32_out, not_33_out);
  and and_18 (and_18_out, not_34_out, ABCD[1], not_35_out);
  and and_19 (and_19_out, not_36_out, not_37_out, not_38_out);
  and and_20 (and_20_out, not_39_out, ABCD[2], not_40_out);
  and and_21 (and_21_out, not_41_out, ABCD[2], not_42_out);
  and and_22 (and_22_out, ABCD[3], not_43_out, not_44_out);
  and and_23 (and_23_out, not_45_out, ABCD[1]);
  and and_24 (and_24_out, ABCD[2], not_46_out);
  and and_25 (and_25_out, ABCD[2], not_47_out);
  or or_1 (a, and_1_out, and_2_out, and_3_out, and_4_out);
  or or_2 (b, and_5_out, and_6_out, and_7_out, and_8_out);
  or or_3 (c, and_9_out, and_10_out, and_11_out);
  or or_4 (d, and_12_out, and_13_out, and_14_out, and_15_out, and_16_out);
  or or_5 (e, and_17_out, and_18_out);
  or or_6 (f, and_19_out, and_20_out, and_21_out, and_22_out);
  or or_7 (g, and_23_out, and_24_out, and_25_out, ABCD[3]);
endmodule

module Display_7_Seg2 (
  input  A,
  input  B,
  input  C,
  input  D,
  output a_2,
  output b_2,
  output c_2,
  output d_2,
  output e,
  output f,
  output g
);

  wire and_1_out, and_2_out, and_3_out, and_4_out, and_5_out, and_6_out, and_7_out, and_8_out, and_9_out,
       and_10_out, and_11_out, and_12_out, and_13_out, and_14_out, and_15_out, and_16_out, and_17_out,
       and_18_out, and_19_out, and_20_out, and_21_out, and_22_out, and_23_out, and_24_out, and_25_out,
       not_1_out, not_2_out, not_3_out, not_4_out, not_5_out, not_6_out, not_7_out, not_8_out, not_9_out,
       not_10_out, not_11_out, not_12_out, not_13_out, not_14_out, not_15_out, not_16_out, not_17_out,
       not_18_out, not_19_out, not_20_out, not_21_out, not_22_out, not_23_out, not_24_out, not_25_out,
       not_26_out, not_27_out, not_28_out, not_29_out, not_30_out, not_31_out, not_32_out, not_33_out,
       not_34_out, not_35_out, not_36_out, not_37_out, not_38_out, not_39_out, not_40_out, not_41_out,
       not_42_out, not_43_out, not_44_out, not_45_out, not_46_out, not_47_out;

  not not_1 (not_1_out, A);
  not not_2 (not_2_out, B);
  not not_3 (not_3_out, D);
  not not_4 (not_4_out, A);
  not not_5 (not_5_out, A);
  not not_6 (not_6_out, B);
  not not_7 (not_7_out, C);
  not not_8 (not_8_out, A);
  not not_9 (not_9_out, B);
  not not_10 (not_10_out, A);
  not not_11 (not_11_out, C);
  not not_12 (not_12_out, D);
  not not_13 (not_13_out, B);
  not not_14 (not_14_out, C);
  not not_15 (not_15_out, A);
  not not_16 (not_16_out, B);
  not not_17 (not_17_out, C);
  not not_18 (not_18_out, A);
  not not_19 (not_19_out, A);
  not not_20 (not_20_out, A);
  not not_21 (not_21_out, B);
  not not_22 (not_22_out, D);
  not not_23 (not_23_out, A);
  not not_24 (not_24_out, B);
  not not_25 (not_25_out, A);
  not not_26 (not_26_out, D);
  not not_27 (not_27_out, A);
  not not_28 (not_28_out, C);
  not not_29 (not_29_out, B);
  not not_30 (not_30_out, C);
  not not_31 (not_31_out, B);
  not not_32 (not_32_out, C);
  not not_33 (not_33_out, D);
  not not_34 (not_34_out, A);
  not not_35 (not_35_out, D);
  not not_36 (not_36_out, A);
  not not_37 (not_37_out, C);
  not not_38 (not_38_out, D);
  not not_39 (not_39_out, A);
  not not_40 (not_40_out, C);
  not not_41 (not_41_out, A);
  not not_42 (not_42_out, D);
  not not_43 (not_43_out, B);
  not not_44 (not_44_out, C);
  not not_45 (not_45_out, B);
  not not_46 (not_46_out, C);
  not not_47 (not_47_out, D);
  and and_1 (and_1_out, not_1_out, not_2_out, not_3_out);
  and and_2 (and_2_out, not_4_out, C);
  and and_3 (and_3_out, not_5_out, B, D);
  and and_4 (and_4_out, A, not_6_out, not_7_out);
  and and_5 (and_5_out, not_8_out, not_9_out);
  and and_6 (and_6_out, not_10_out, not_11_out, not_12_out);
  and and_7 (and_7_out, not_13_out, not_14_out);
  and and_8 (and_8_out, not_15_out, C, D);
  and and_9 (and_9_out, not_16_out, not_17_out);
  and and_10 (and_10_out, not_18_out, D);
  and and_11 (and_11_out, not_19_out, B);
  and and_12 (and_12_out, not_20_out, not_21_out, not_22_out);
  and and_13 (and_13_out, not_23_out, not_24_out, C);
  and and_14 (and_14_out, not_25_out, C, not_26_out);
  and and_15 (and_15_out, not_27_out, B, not_28_out, D);
  and and_16 (and_16_out, A, not_29_out, not_30_out);
  and and_17 (and_17_out, not_31_out, not_32_out, not_33_out);
  and and_18 (and_18_out, not_34_out, C, not_35_out);
  and and_19 (and_19_out, not_36_out, not_37_out, not_38_out);
  and and_20 (and_20_out, not_39_out, B, not_40_out);
  and and_21 (and_21_out, not_41_out, B, not_42_out);
  and and_22 (and_22_out, A, not_43_out, not_44_out);
  and and_23 (and_23_out, not_45_out, C);
  and and_24 (and_24_out, B, not_46_out);
  and and_25 (and_25_out, B, not_47_out);
  or or_1 (a_2, and_1_out, and_2_out, and_3_out, and_4_out);
  or or_2 (b_2, and_5_out, and_6_out, and_7_out, and_8_out);
  or or_3 (c_2, and_9_out, and_10_out, and_11_out);
  or or_4 (d_2, and_12_out, and_13_out, and_14_out, and_15_out, and_16_out);
  or or_5 (e, and_17_out, and_18_out);
  or or_6 (f, and_19_out, and_20_out, and_21_out, and_22_out);
  or or_7 (g, and_23_out, and_24_out, and_25_out, A);
endmodule
