// Logisim project Somador Carry Look-a-Head.circ as structural Verilog: 3 circuits, main circuit main
module main (
  input  [7:0] A,
  input  [7:0] B,
  input  Op,
  output Cout8,
  output [7:0] S
);

  wire cout_1_cout1, cout_1_cout2, cout_1_cout3, cout_1_cout4, cout_1_cout5, cout_1_cout6, cout_1_cout7,
       cout_1_p0, cout_1_p1, cout_1_p2, cout_1_p3, cout_1_p4, cout_1_p5, cout_1_p6, cout_1_p7;
  wire [7:0] distribuidor_1_out_2, xor_1_out;

  // Probe on B
  // Probe on S
  // Probe on A
  assign xor_1_out = B ^ distribuidor_1_out_2;  // XOR_Gate xor_1, 8 bits wide
  Distribuidor distribuidor_1 (.in_1(Op), .out_2(distribuidor_1_out_2));
  xor xor_2 (S[7], cout_1_p7, cout_1_cout7);
  xor xor_3 (S[6], cout_1_p6, cout_1_cout6);
  xor xor_4 (S[5], cout_1_p5, cout_1_cout5);
  xor xor_5 (S[4], cout_1_p4, cout_1_cout4);
  xor xor_6 (S[3], cout_1_p3, cout_1_cout3);
  xor xor_7 (S[2], cout_1_p2, cout_1_cout2);
  xor xor_8 (S[1], cout_1_p1, cout_1_cout1);
  xor xor_9 (S[0], cout_1_p0, Op);
  Cout cout_1 (
    .A(A[5]), .B(xor_1_out[5]), .A_2(A[0]), .B_2(xor_1_out[0]), .Cin(Op), .A_3(A[1]), .B_3(xor_1_out[1]),
    .A_4(A[2]), .B_4(xor_1_out[2]), .A_5(A[6]), .B_5(xor_1_out[6]), .A_6(A[3]), .B_6(xor_1_out[3]),
    .A_7(A[4]), .A_8(A[7]), .B_7(xor_1_out[4]), .B_8(xor_1_out[7]), .Cout6(cout_1_cout6),
    .Cout1(cout_1_cout1), .Cout2(cout_1_cout2), .Cout3(cout_1_cout3), .Cout7(cout_1_cout7),
    .Cout4(cout_1_cout4), .Cout5(cout_1_cout5), .Cout8(Cout8), .P0(cout_1_p0), .P1(cout_1_p1),
    .P2(cout_1_p2), .P3(cout_1_p3), .P4(cout_1_p4), .P5(cout_1_p5), .P6(cout_1_p6), .P7(cout_1_p7));
endmodule

module Cout (
  input  A,
  input  B,
  input  A_2,
  input  B_2,
  input  Cin,
  input  A_3,
  input  B_3,
  input  A_4,
  input  B_4,
  input  A_5,
  input  B_5,
  input  A_6,
  input  B_6,
  input  A_7,
  input  A_8,
  input  B_7,
  input  B_8,
  output Cout6,
  output Cout1,
  output P5,
  output P0,
  output Cout2,
  output P1,
  output Cout3,
  output Cout7,
  output P6,
  output P2,
  output Cout4,
  output P3,
  output Cout5,
  output P4,
  output Cout8,
  output P7
);

  wire and_1_out, and_2_out, and_3_out, and_4_out, and_5_out, and_6_out, and_7_out, and_8_out, and_9_out,
       and_10_out, and_11_out, and_12_out, and_13_out, and_14_out, and_15_out, and_16_out, and_17_out,
       and_18_out, and_19_out, and_20_out, and_21_out, and_22_out, and_23_out, and_24_out, and_25_out,
       and_26_out, and_27_out, and_28_out, and_29_out, and_30_out, and_31_out, and_32_out, and_33_out,
       and_34_out, and_35_out, and_36_out, G0, G1, G2, G3, G4, G5, G6, G7_out;

  and u_G0 (G0, A_2, B_2);
  xor u_P0 (P0, A_2, B_2);
  and u_G1 (G1, A_3, B_3);
  xor u_P1 (P1, A_3, B_3);
  and u_G2 (G2, A_4, B_4);
  xor u_P2 (P2, A_4, B_4);
  and u_G3 (G3, A_6, B_6);
  xor u_P3 (P3, A_6, B_6);
  and and_1 (and_1_out, P0, Cin);
  and and_2 (and_2_out, P1, G0);
  and and_3 (and_3_out, P1, G0, P2);
  and and_4 (and_4_out, P2, G1);
  and and_5 (and_5_out, G2, P3);
  and and_6 (and_6_out, P3, P2, G1);
  and u_G4 (G4, A_7, B_7);
  xor u_P4 (P4, A_7, B_7);
  or or_1 (Cout1, G0, and_1_out);
  and and_7 (and_7_out, Cin, P0, P1);
  and and_8 (and_8_out, P1, P2, P0, Cin);
  and and_9 (and_9_out, G3, P4);
  and and_10 (and_10_out, P4, P3, G2);
  or or_2 (Cout2, G1, and_7_out, and_2_out);
  and and_11 (and_11_out, P1, P2, G0, P3);
  and and_12 (and_12_out, P3, P2, P1, Cin, P0);
  and and_13 (and_13_out, P4, P3, P2, G1);
  or or_3 (Cout3, G2, and_3_out, and_8_out, and_4_out);
  and and_14 (and_14_out, P4, P3, P2, P1, G0);
  or or_4 (Cout4, G3, and_5_out, and_11_out, and_12_out, and_6_out);
  and and_15 (and_15_out, P4, P3, P2, P1, P0, Cin);
  or or_5 (Cout5, G4, and_9_out, and_10_out, and_13_out, and_14_out, and_15_out);
  and u_G5 (G5, A, B);
  xor u_P5 (P5, A, B);
  and u_G6 (G6, A_5, B_5);
  xor u_P6 (P6, A_5, B_5);
  and G7 (G7_out, A_8, B_8);
  xor u_P7 (P7, A_8, B_8);
  and and_16 (and_16_out, G4, P5);
  and and_17 (and_17_out, P5, P4, G3);
  and and_18 (and_18_out, G5, P6);
  and and_19 (and_19_out, P6, P5, G4);
  and and_20 (and_20_out, G6, P7);
  and and_21 (and_21_out, P7, P6, G5);
  and and_22 (and_22_out, P5, P4, P3, G2);
  and and_23 (and_23_out, P5, P4, P3, P2, G1);
  and and_24 (and_24_out, P6, P5, P4, G3);
  and and_25 (and_25_out, P7, P6, P5, G4);
  and and_26 (and_26_out, P6, P5, P4, P3, G2);
  and and_27 (and_27_out, P7, P6, P5, P4, G3);
  and and_28 (and_28_out, P5, P4, P3, P2, P1, G0);
  and and_29 (and_29_out, P6, P5, P4, P3, P2, G1);
  and and_30 (and_30_out, P7, P6, P5, P4, P3, G2);
  and and_31 (and_31_out, P5, P4, P3, P2, P1, P0, Cin);
  or or_6 (Cout6, G5, and_16_out, and_17_out, and_22_out, and_23_out, and_28_out, and_31_out);
  and and_32 (and_32_out, P6, P5, P4, P3, P2, P1, G0);
  and and_33 (and_33_out, P7, P6, P5, P4, P3, P2, G1);
  and and_34 (and_34_out, P6, P5, P4, P3, P2, P1, P0, Cin);
  and and_35 (and_35_out, P7, P6, P5, P4, P3, P2, P1, G0);
  or or_7 (Cout7, G6, and_18_out, and_19_out, and_24_out, and_26_out, and_29_out, and_32_out, and_34_out);
  and and_36 (and_36_out, P7, P6, P5, P4, P3, P2, P1, P0, Cin);
  or or_8 (Cout8, G7_out, and_20_out, and_21_out, and_25_out, and_27_out, and_30_out, and_33_out, and_35_out, and_36_out);

  // Other names for the same wires on the sheet: C0 = Cin
endmodule

module Distribuidor (
  input  in_1,
  output [7:0] out_2
);


  assign out_2 = {8{in_1}};
endmodule
