// Logisim project Somador_Subtrator.circ as structural Verilog: 4 circuits, main circuit main
module main (
  input  [7:0] A,
  input  [7:0] B,
  input  Op,
  output out_4,
  output [7:0] S
);

  wire somador_1bit_2_cout, somador_1bit_3_cout, somador_1bit_4_cout, somador_1bit_5_cout,
       somador_1bit_6_cout, somador_1bit_7_cout, somador_1bit_8_cout;
  wire [7:0] distribuidor_1_out_2, xor_1_out;

  Distribuidor distribuidor_1 (.in_1(Op), .out_2(distribuidor_1_out_2));
  assign xor_1_out = B ^ distribuidor_1_out_2;  // XOR_Gate xor_1, 8 bits wide
  Somador_1bit somador_1bit_1 (.Cout(out_4), .S(S[7]), .A(A[7]), .B(xor_1_out[7]), .Cin(somador_1bit_3_cout));
  Somador_1bit somador_1bit_2 (
    .Cout(somador_1bit_2_cout), .S(S[5]), .A(A[5]), .B(xor_1_out[5]), .Cin(somador_1bit_4_cout));
  Somador_1bit somador_1bit_3 (
    .Cout(somador_1bit_3_cout), .S(S[6]), .A(A[6]), .B(xor_1_out[6]), .Cin(somador_1bit_2_cout));
  Somador_1bit somador_1bit_4 (
    .Cout(somador_1bit_4_cout), .S(S[4]), .A(A[4]), .B(xor_1_out[4]), .Cin(somador_1bit_5_cout));
  Somador_1bit somador_1bit_5 (
    .Cout(somador_1bit_5_cout), .S(S[3]), .A(A[3]), .B(xor_1_out[3]), .Cin(somador_1bit_6_cout));
  Somador_1bit somador_1bit_6 (
    .Cout(somador_1bit_6_cout), .S(S[2]), .A(A[2]), .B(xor_1_out[2]), .Cin(somador_1bit_7_cout));
  Somador_1bit somador_1bit_7 (
    .Cout(somador_1bit_7_cout), .S(S[1]), .A(A[1]), .B(xor_1_out[1]), .Cin(somador_1bit_8_cout));
  Somador_1bit somador_1bit_8 (.Cout(somador_1bit_8_cout), .S(S[0]), .A(A[0]), .B(xor_1_out[0]), .Cin(Op));
endmodule

module Somador_1bit (
  input  A,
  input  B,
  input  Cin,
  output Cout,
  output S
);

  wire and_1_out, and_2_out, and_3_out, xor_1_out;

  and and_1 (and_1_out, A, B);
  and and_2 (and_2_out, A, Cin);
  and and_3 (and_3_out, B, Cin);
  xor xor_1 (xor_1_out, A, B);
  or or_1 (Cout, and_1_out, and_2_out, and_3_out);
  xor xor_2 (S, Cin, xor_1_out);
endmodule

module Subtrator_1_bit (
  input  A,
  input  B,
  input  Cin,
  output Cout,
  output S
);

  wire and_1_out, and_2_out, and_3_out, xor_1_out;

  and and_1 (and_1_out, ~A, B);  // AND_Gate
  and and_2 (and_2_out, A, Cin);
  and and_3 (and_3_out, ~B, Cin);  // AND_Gate
  xor xor_1 (xor_1_out, A, B);
  or or_1 (Cout, and_1_out, and_2_out, and_3_out);
  xor xor_2 (S, Cin, xor_1_out);
endmodule

module Distribuidor (
  input  in_1,
  output [7:0] out_2
);


  assign out_2 = {8{in_1}};
endmodule
