// Logisim project pczin.circ as structural Verilog: 8 circuits, main circuit main
module main (
  input  [10:0] in_1,
  input  in_2
);

  wire Ck;
  wire [2:0] contador_1_num;
  wire [7:0] A, ula_1_out_4;
  wire [10:0] memoria_1_out_4;

  contador contador_1 (.in_1(Ck), .Num(contador_1_num));  // open: R_W
  Clock clock_1 (.out(Ck));
  // Probe on contador_1_num
  memoria memoria_1 (.\Endereço (contador_1_num), .out_4(memoria_1_out_4), .Entrada(in_1), .WE(in_2));
  // Probe on memoria_1_out_4[7:0]
  ULA ula_1 (.A(A), .B(memoria_1_out_4[7:0]), .in_3(memoria_1_out_4[10:8]), .out_4(ula_1_out_4));
  // Probe on memoria_1_out_4[10:8]
  registrador registrador_1 (.in_1(ula_1_out_4), .out_3(A), .WE(Ck));
  // Probe on A
  // Probe on A

  // Notes on the sheet:
  //   000 - AND
  //   001- OR
  //   010 - XOR
  //   011 - ADD
  //   100 - SUB
  //   101 - MUL
  //   110 - DIV
  //   111 - MOD
endmodule

// Memória
module memoria (
  input  [2:0] \Endereço ,
  input  [10:0] Entrada,
  input  WE,
  output [10:0] out_4
);

  wire and_1_out, and_2_out, and_3_out, and_4_out, and_5_out, and_6_out, and_7_out, and_8_out, and_9_out,
       and_10_out, and_11_out, and_12_out, and_13_out, and_14_out, and_15_out, and_16_out, and_17_out,
       and_18_out, and_19_out, and_20_out, and_21_out, and_22_out, and_23_out, and_24_out, and_25_out,
       and_26_out, and_27_out, and_28_out, and_29_out, and_30_out, and_31_out, and_32_out, and_33_out,
       and_34_out, and_35_out, and_36_out, and_37_out, and_38_out, and_39_out, and_40_out, and_41_out,
       and_42_out, and_43_out, and_44_out, and_45_out, and_46_out, and_47_out, and_48_out, and_49_out,
       and_50_out, and_51_out, and_52_out, and_53_out, and_54_out, and_55_out, and_56_out, and_57_out,
       and_58_out, and_59_out, and_60_out, and_61_out, and_62_out, and_63_out, and_64_out, and_65_out,
       and_66_out, and_67_out, and_68_out, and_69_out, and_70_out, and_71_out, and_72_out, and_73_out,
       and_74_out, and_75_out, and_76_out, and_77_out, and_78_out, and_79_out, and_80_out, and_81_out,
       and_82_out, and_83_out, and_84_out, and_85_out, and_86_out, and_87_out, and_88_out, and_89_out,
       and_90_out, and_91_out, and_92_out, and_93_out, and_94_out, and_95_out, and_96_out, and_97_out,
       and_98_out, and_99_out, and_100_out, and_101_out, and_102_out, and_103_out, and_104_out, d_ff_1_q,
       d_ff_2_q, d_ff_3_q, d_ff_4_q, d_ff_5_q, d_ff_6_q, d_ff_7_q, d_ff_8_q, d_ff_9_q, d_ff_10_q, d_ff_11_q,
       d_ff_12_q, d_ff_13_q, d_ff_14_q, d_ff_15_q, d_ff_16_q, d_ff_17_q, d_ff_18_q, d_ff_19_q, d_ff_20_q,
       d_ff_21_q, d_ff_22_q, d_ff_23_q, d_ff_24_q, d_ff_25_q, d_ff_26_q, d_ff_27_q, d_ff_28_q, d_ff_29_q,
       d_ff_30_q, d_ff_31_q, d_ff_32_q, d_ff_33_q, d_ff_34_q, d_ff_35_q, d_ff_36_q, d_ff_37_q, d_ff_38_q,
       d_ff_39_q, d_ff_40_q, d_ff_41_q, d_ff_42_q, d_ff_43_q, d_ff_44_q, d_ff_45_q, d_ff_46_q, d_ff_47_q,
       d_ff_48_q, d_ff_49_q, d_ff_50_q, d_ff_51_q, d_ff_52_q, d_ff_53_q, d_ff_54_q, d_ff_55_q, d_ff_56_q,
       d_ff_57_q, d_ff_58_q, d_ff_59_q, d_ff_60_q, d_ff_61_q, d_ff_62_q, d_ff_63_q, d_ff_64_q, d_ff_65_q,
       d_ff_66_q, d_ff_67_q, d_ff_68_q, d_ff_69_q, d_ff_70_q, d_ff_71_q, d_ff_72_q, d_ff_73_q, d_ff_74_q,
       d_ff_75_q, d_ff_76_q, d_ff_77_q, d_ff_78_q, d_ff_79_q, d_ff_80_q, d_ff_81_q, d_ff_82_q, d_ff_83_q,
       d_ff_84_q, d_ff_85_q, d_ff_86_q, d_ff_87_q, d_ff_88_q, undriven;

  and and_1 (and_1_out, ~\Endereço [2], ~\Endereço [1], ~\Endereço [0]);  // AND_Gate
  and and_2 (and_2_out, ~\Endereço [2], ~\Endereço [1], \Endereço [0]);  // AND_Gate
  and and_3 (and_3_out, ~\Endereço [2], \Endereço [1], ~\Endereço [0]);  // AND_Gate
  and and_4 (and_4_out, ~\Endereço [2], \Endereço [1], \Endereço [0]);  // AND_Gate
  and and_5 (and_5_out, \Endereço [2], ~\Endereço [1], ~\Endereço [0]);  // AND_Gate
  and and_6 (and_6_out, \Endereço [2], ~\Endereço [1], \Endereço [0]);  // AND_Gate
  and and_7 (and_7_out, \Endereço [2], \Endereço [1], ~\Endereço [0]);  // AND_Gate
  and and_8 (and_8_out, \Endereço [2], \Endereço [1], \Endereço [0]);
  and and_9 (and_9_out, and_1_out, WE);
  and and_10 (and_10_out, and_2_out, WE);
  and and_11 (and_11_out, and_3_out, WE);
  and and_12 (and_12_out, and_4_out, WE);
  and and_13 (and_13_out, and_5_out, WE);
  and and_14 (and_14_out, and_6_out, WE);
  and and_15 (and_15_out, and_7_out, WE);
  and and_16 (and_16_out, and_8_out, WE);
  D_Flip_Flop d_ff_1 (.clk(and_9_out), .D(Entrada[10]), .Q(d_ff_1_q));  // open: Qn, preset, en, reset
  D_Flip_Flop d_ff_2 (.clk(and_10_out), .D(Entrada[10]), .Q(d_ff_2_q));  // open: Qn, preset, en, reset
  D_Flip_Flop d_ff_3 (.clk(and_11_out), .D(Entrada[10]), .Q(d_ff_3_q));  // open: Qn, preset, en, reset
  D_Flip_Flop d_ff_4 (.clk(and_12_out), .D(Entrada[10]), .Q(d_ff_4_q));  // open: Qn, preset, en, reset
  D_Flip_Flop d_ff_5 (.clk(and_13_out), .D(Entrada[10]), .Q(d_ff_5_q));  // open: Qn, preset, en, reset
  D_Flip_Flop d_ff_6 (.clk(and_14_out), .D(Entrada[10]), .Q(d_ff_6_q));  // open: Qn, preset, en, reset
  D_Flip_Flop d_ff_7 (.clk(and_15_out), .D(Entrada[10]), .Q(d_ff_7_q));  // open: Qn, preset, en, reset
  D_Flip_Flop d_ff_8 (.clk(and_16_out), .D(Entrada[10]), .Q(d_ff_8_q));  // open: Qn, preset, en, reset
  and and_17 (and_17_out, d_ff_8_q, and_8_out);
  and and_18 (and_18_out, d_ff_1_q, and_1_out);
  and and_19 (and_19_out, d_ff_2_q, and_2_out);
  and and_20 (and_20_out, d_ff_3_q, and_3_out);
  and and_21 (and_21_out, d_ff_4_q, and_4_out);
  and and_22 (and_22_out, d_ff_5_q, and_5_out);
  and and_23 (and_23_out, d_ff_6_q, and_6_out);
  and and_24 (and_24_out, d_ff_7_q, and_7_out);
  or or_1 (out_4[10], and_17_out, and_24_out, and_23_out, and_22_out, and_21_out, and_20_out, and_19_out, and_18_out);
  D_Flip_Flop d_ff_9 (.clk(and_9_out), .D(Entrada[9]), .Q(d_ff_9_q));  // open: Qn, preset, en, reset
  D_Flip_Flop d_ff_10 (.clk(and_10_out), .D(Entrada[9]), .Q(d_ff_10_q));  // open: Qn, preset, en, reset
  and and_25 (and_25_out, d_ff_10_q, and_2_out);
  D_Flip_Flop d_ff_11 (.clk(and_11_out), .D(Entrada[9]), .Q(d_ff_11_q));  // open: Qn, preset, en, reset
  and and_26 (and_26_out, d_ff_11_q, and_3_out);
  D_Flip_Flop d_ff_12 (.clk(and_12_out), .D(Entrada[9]), .Q(d_ff_12_q));  // open: Qn, preset, en, reset
  and and_27 (and_27_out, d_ff_12_q, and_4_out);
  D_Flip_Flop d_ff_13 (.clk(and_13_out), .D(Entrada[9]), .Q(d_ff_13_q));  // open: Qn, preset, en, reset
  and and_28 (and_28_out, d_ff_13_q, and_5_out);
  D_Flip_Flop d_ff_14 (.clk(and_14_out), .D(Entrada[9]), .Q(d_ff_14_q));  // open: Qn, preset, en, reset
  and and_29 (and_29_out, d_ff_14_q, and_6_out);
  D_Flip_Flop d_ff_15 (.clk(and_15_out), .D(Entrada[9]), .Q(d_ff_15_q));  // open: Qn, preset, en, reset
  and and_30 (and_30_out, d_ff_15_q, and_7_out);
  D_Flip_Flop d_ff_16 (.clk(and_16_out), .D(Entrada[9]), .Q(d_ff_16_q));  // open: Qn, preset, en, reset
  and and_31 (and_31_out, d_ff_16_q, and_8_out);
  and and_32 (and_32_out, d_ff_9_q, and_1_out);
  or or_2 (out_4[9], and_31_out, and_30_out, and_29_out, and_28_out, and_27_out, and_26_out, and_25_out, and_32_out);
  D_Flip_Flop d_ff_17 (.clk(and_9_out), .D(Entrada[8]), .Q(d_ff_17_q));  // open: Qn, preset, en, reset
  and and_33 (and_33_out, d_ff_17_q, and_1_out);
  D_Flip_Flop d_ff_18 (.clk(and_10_out), .D(Entrada[8]), .Q(d_ff_18_q));  // open: Qn, preset, en, reset
  and and_34 (and_34_out, d_ff_18_q, and_2_out);
  D_Flip_Flop d_ff_19 (.clk(and_11_out), .D(Entrada[8]), .Q(d_ff_19_q));  // open: Qn, preset, en, reset
  and and_35 (and_35_out, d_ff_19_q, and_3_out);
  D_Flip_Flop d_ff_20 (.clk(and_12_out), .D(Entrada[8]), .Q(d_ff_20_q));  // open: Qn, preset, en, reset
  and and_36 (and_36_out, d_ff_20_q, and_4_out);
  D_Flip_Flop d_ff_21 (.clk(and_13_out), .D(Entrada[8]), .Q(d_ff_21_q));  // open: Qn, preset, en, reset
  and and_37 (and_37_out, d_ff_21_q, and_5_out);
  D_Flip_Flop d_ff_22 (.clk(and_14_out), .D(Entrada[8]), .Q(d_ff_22_q));  // open: Qn, preset, en, reset
  and and_38 (and_38_out, d_ff_22_q, and_6_out);
  D_Flip_Flop d_ff_23 (.clk(and_15_out), .D(Entrada[8]), .Q(d_ff_23_q));  // open: Qn, preset, en, reset
  and and_39 (and_39_out, d_ff_23_q, and_7_out);
  D_Flip_Flop d_ff_24 (.clk(and_16_out), .D(Entrada[8]), .Q(d_ff_24_q));  // open: Qn, preset, en, reset
  and and_40 (and_40_out, d_ff_24_q, and_8_out);
  or or_3 (out_4[8], and_40_out, and_39_out, and_38_out, and_37_out, and_36_out, and_35_out, and_34_out, and_33_out);
  D_Flip_Flop d_ff_25 (.clk(and_9_out), .D(Entrada[7]), .Q(d_ff_25_q));  // open: Qn, preset, en, reset
  and and_41 (and_41_out, d_ff_25_q, and_1_out);
  D_Flip_Flop d_ff_26 (.clk(and_10_out), .D(Entrada[7]), .Q(d_ff_26_q));  // open: Qn, preset, en, reset
  and and_42 (and_42_out, d_ff_26_q, and_2_out);
  D_Flip_Flop d_ff_27 (.clk(and_11_out), .D(Entrada[7]), .Q(d_ff_27_q));  // open: Qn, preset, en, reset
  and and_43 (and_43_out, d_ff_27_q, and_3_out);
  D_Flip_Flop d_ff_28 (.clk(and_12_out), .D(Entrada[7]), .Q(d_ff_28_q));  // open: Qn, preset, en, reset
  and and_44 (and_44_out, d_ff_28_q, and_4_out);
  D_Flip_Flop d_ff_29 (.clk(and_13_out), .D(Entrada[7]), .Q(d_ff_29_q));  // open: Qn, preset, en, reset
  and and_45 (and_45_out, d_ff_29_q, and_5_out);
  D_Flip_Flop d_ff_30 (.clk(and_14_out), .D(Entrada[7]), .Q(d_ff_30_q));  // open: Qn, preset, en, reset
  and and_46 (and_46_out, d_ff_30_q, and_6_out);
  D_Flip_Flop d_ff_31 (.clk(and_15_out), .D(Entrada[7]), .Q(d_ff_31_q));  // open: Qn, preset, en, reset
  and and_47 (and_47_out, d_ff_31_q, and_7_out);
  D_Flip_Flop d_ff_32 (.clk(and_16_out), .D(Entrada[7]), .Q(d_ff_32_q));  // open: Qn, preset, en, reset
  and and_48 (and_48_out, d_ff_32_q, and_8_out);
  or or_4 (out_4[7], and_48_out, and_47_out, and_46_out, and_45_out, and_44_out, and_43_out, and_42_out, and_41_out);
  D_Flip_Flop d_ff_33 (.clk(and_9_out), .D(Entrada[6]), .Q(d_ff_33_q));  // open: Qn, preset, en, reset
  and and_49 (and_49_out, d_ff_33_q, and_1_out);
  D_Flip_Flop d_ff_34 (.clk(and_10_out), .D(Entrada[6]), .Q(d_ff_34_q));  // open: Qn, preset, en, reset
  and and_50 (and_50_out, d_ff_34_q, and_2_out);
  D_Flip_Flop d_ff_35 (.clk(and_11_out), .D(Entrada[6]), .Q(d_ff_35_q));  // open: Qn, preset, en, reset
  and and_51 (and_51_out, d_ff_35_q, and_3_out);
  D_Flip_Flop d_ff_36 (.clk(and_12_out), .D(Entrada[6]), .Q(d_ff_36_q));  // open: Qn, preset, en, reset
  and and_52 (and_52_out, d_ff_36_q, and_4_out);
  D_Flip_Flop d_ff_37 (.clk(and_13_out), .D(Entrada[6]), .Q(d_ff_37_q));  // open: Qn, preset, en, reset
  and and_53 (and_53_out, d_ff_37_q, and_5_out);
  D_Flip_Flop d_ff_38 (.clk(and_14_out), .D(Entrada[6]), .Q(d_ff_38_q));  // open: Qn, preset, en, reset
  and and_54 (and_54_out, d_ff_38_q, and_6_out);
  D_Flip_Flop d_ff_39 (.clk(and_15_out), .D(Entrada[6]), .Q(d_ff_39_q));  // open: Qn, preset, en, reset
  and and_55 (and_55_out, d_ff_39_q, and_7_out);
  D_Flip_Flop d_ff_40 (.clk(and_16_out), .D(Entrada[6]), .Q(d_ff_40_q));  // open: Qn, preset, en, reset
  and and_56 (and_56_out, d_ff_40_q, and_8_out);
  or or_5 (out_4[6], and_56_out, and_55_out, and_54_out, and_53_out, and_52_out, and_51_out, and_50_out, and_49_out);
  D_Flip_Flop d_ff_41 (.clk(and_9_out), .D(Entrada[5]), .Q(d_ff_41_q));  // open: Qn, preset, en, reset
  and and_57 (and_57_out, d_ff_41_q, and_1_out);
  D_Flip_Flop d_ff_42 (.clk(and_10_out), .D(Entrada[5]), .Q(d_ff_42_q));  // open: Qn, preset, en, reset
  and and_58 (and_58_out, d_ff_42_q, and_2_out);
  D_Flip_Flop d_ff_43 (.clk(and_11_out), .D(Entrada[5]), .Q(d_ff_43_q));  // open: Qn, preset, en, reset
  and and_59 (and_59_out, d_ff_43_q, and_3_out);
  D_Flip_Flop d_ff_44 (.clk(and_12_out), .D(Entrada[5]), .Q(d_ff_44_q));  // open: Qn, preset, en, reset
  and and_60 (and_60_out, d_ff_44_q, and_4_out);
  D_Flip_Flop d_ff_45 (.clk(and_13_out), .D(Entrada[5]), .Q(d_ff_45_q));  // open: Qn, preset, en, reset
  and and_61 (and_61_out, d_ff_45_q, and_5_out);
  D_Flip_Flop d_ff_46 (.clk(and_14_out), .D(Entrada[5]), .Q(d_ff_46_q));  // open: Qn, preset, en, reset
  and and_62 (and_62_out, d_ff_46_q, and_6_out);
  D_Flip_Flop d_ff_47 (.clk(and_15_out), .D(Entrada[5]), .Q(d_ff_47_q));  // open: Qn, preset, en, reset
  and and_63 (and_63_out, d_ff_47_q, and_7_out);
  D_Flip_Flop d_ff_48 (.clk(and_16_out), .D(Entrada[5]), .Q(d_ff_48_q));  // open: Qn, preset, en, reset
  and and_64 (and_64_out, d_ff_48_q, and_8_out);
  or or_6 (out_4[5], and_64_out, and_63_out, and_62_out, and_61_out, and_60_out, and_59_out, and_58_out, and_57_out);
  D_Flip_Flop d_ff_49 (.clk(and_9_out), .D(Entrada[4]), .Q(d_ff_49_q));  // open: Qn, preset, en, reset
  and and_65 (and_65_out, d_ff_49_q, and_1_out);
  D_Flip_Flop d_ff_50 (.clk(and_10_out), .D(Entrada[4]), .Q(d_ff_50_q));  // open: Qn, preset, en, reset
  and and_66 (and_66_out, d_ff_50_q, and_2_out);
  D_Flip_Flop d_ff_51 (.clk(and_11_out), .D(Entrada[4]), .Q(d_ff_51_q));  // open: Qn, preset, en, reset
  and and_67 (and_67_out, d_ff_51_q, and_3_out);
  D_Flip_Flop d_ff_52 (.clk(and_12_out), .D(Entrada[4]), .Q(d_ff_52_q));  // open: Qn, preset, en, reset
  and and_68 (and_68_out, d_ff_52_q, and_4_out);
  D_Flip_Flop d_ff_53 (.clk(and_13_out), .D(Entrada[4]), .Q(d_ff_53_q));  // open: Qn, preset, en, reset
  and and_69 (and_69_out, d_ff_53_q, and_5_out);
  D_Flip_Flop d_ff_54 (.clk(and_14_out), .D(Entrada[4]), .Q(d_ff_54_q));  // open: Qn, preset, en, reset
  and and_70 (and_70_out, d_ff_54_q, and_6_out);
  D_Flip_Flop d_ff_55 (.clk(and_15_out), .D(Entrada[4]), .Q(d_ff_55_q));  // open: Qn, preset, en, reset
  and and_71 (and_71_out, d_ff_55_q, and_7_out);
  D_Flip_Flop d_ff_56 (.clk(and_16_out), .D(Entrada[4]), .Q(d_ff_56_q));  // open: Qn, preset, en, reset
  and and_72 (and_72_out, d_ff_56_q, and_8_out);
  or or_7 (out_4[4], and_72_out, and_71_out, and_70_out, and_69_out, and_68_out, and_67_out, and_66_out, and_65_out);
  D_Flip_Flop d_ff_57 (.clk(and_9_out), .D(Entrada[3]), .Q(d_ff_57_q));  // open: Qn, preset, en, reset
  and and_73 (and_73_out, d_ff_57_q, and_1_out);
  D_Flip_Flop d_ff_58 (.clk(and_10_out), .D(Entrada[3]), .Q(d_ff_58_q));  // open: Qn, preset, en, reset
  and and_74 (and_74_out, d_ff_58_q, and_2_out);
  D_Flip_Flop d_ff_59 (.clk(and_11_out), .D(Entrada[3]), .Q(d_ff_59_q));  // open: Qn, preset, en, reset
  and and_75 (and_75_out, d_ff_59_q, and_3_out);
  D_Flip_Flop d_ff_60 (.clk(and_12_out), .D(Entrada[3]), .Q(d_ff_60_q));  // open: Qn, preset, en, reset
  and and_76 (and_76_out, d_ff_60_q, and_4_out);
  D_Flip_Flop d_ff_61 (.clk(and_13_out), .D(Entrada[3]), .Q(d_ff_61_q));  // open: Qn, preset, en, reset
  and and_77 (and_77_out, d_ff_61_q, and_5_out);
  D_Flip_Flop d_ff_62 (.clk(and_14_out), .D(Entrada[3]), .Q(d_ff_62_q));  // open: Qn, preset, en, reset
  and and_78 (and_78_out, d_ff_62_q, and_6_out);
  D_Flip_Flop d_ff_63 (.clk(and_15_out), .D(Entrada[3]), .Q(d_ff_63_q));  // open: Qn, preset, en, reset
  and and_79 (and_79_out, d_ff_63_q, and_7_out);
  D_Flip_Flop d_ff_64 (.clk(and_16_out), .D(Entrada[3]), .Q(d_ff_64_q));  // open: Qn, preset, en, reset
  and and_80 (and_80_out, d_ff_64_q, and_8_out);
  or or_8 (out_4[3], and_80_out, and_79_out, and_78_out, and_77_out, and_76_out, and_75_out, and_74_out, and_73_out);
  D_Flip_Flop d_ff_65 (.clk(and_9_out), .D(Entrada[2]), .Q(d_ff_65_q));  // open: Qn, preset, en, reset
  and and_81 (and_81_out, d_ff_65_q, and_1_out);
  D_Flip_Flop d_ff_66 (.clk(and_10_out), .D(Entrada[2]), .Q(d_ff_66_q));  // open: Qn, preset, en, reset
  and and_82 (and_82_out, d_ff_66_q, and_2_out);
  D_Flip_Flop d_ff_67 (.clk(and_11_out), .D(Entrada[2]), .Q(d_ff_67_q));  // open: Qn, preset, en, reset
  and and_83 (and_83_out, d_ff_67_q, and_3_out);
  D_Flip_Flop d_ff_68 (.clk(and_12_out), .D(Entrada[2]), .Q(d_ff_68_q));  // open: Qn, preset, en, reset
  and and_84 (and_84_out, d_ff_68_q, and_4_out);
  D_Flip_Flop d_ff_69 (.clk(and_13_out), .D(Entrada[2]), .Q(d_ff_69_q));  // open: Qn, preset, en, reset
  and and_85 (and_85_out, d_ff_69_q, and_5_out);
  D_Flip_Flop d_ff_70 (.clk(and_14_out), .D(Entrada[2]), .Q(d_ff_70_q));  // open: Qn, preset, en, reset
  and and_86 (and_86_out, d_ff_70_q, and_6_out);
  D_Flip_Flop d_ff_71 (.clk(and_15_out), .D(Entrada[2]), .Q(d_ff_71_q));  // open: Qn, preset, en, reset
  and and_87 (and_87_out, d_ff_71_q, and_7_out);
  D_Flip_Flop d_ff_72 (.clk(and_16_out), .D(Entrada[2]), .Q(d_ff_72_q));  // open: Qn, preset, en, reset
  and and_88 (and_88_out, d_ff_72_q, and_8_out);
  or or_9 (out_4[2], and_88_out, and_87_out, and_86_out, and_85_out, and_84_out, and_83_out, and_82_out, and_81_out);
  D_Flip_Flop d_ff_73 (.clk(and_9_out), .D(Entrada[1]), .Q(d_ff_73_q));  // open: Qn, preset, en, reset
  and and_89 (and_89_out, d_ff_73_q, and_1_out);
  D_Flip_Flop d_ff_74 (.clk(and_10_out), .D(Entrada[1]), .Q(d_ff_74_q));  // open: Qn, preset, en, reset
  and and_90 (and_90_out, d_ff_74_q, and_2_out);
  D_Flip_Flop d_ff_75 (.clk(and_11_out), .D(Entrada[1]), .Q(d_ff_75_q));  // open: Qn, preset, en, reset
  and and_91 (and_91_out, d_ff_75_q, and_3_out);
  D_Flip_Flop d_ff_76 (.clk(and_12_out), .D(Entrada[1]), .Q(d_ff_76_q));  // open: Qn, preset, en, reset
  and and_92 (and_92_out, d_ff_76_q, and_4_out);
  D_Flip_Flop d_ff_77 (.clk(and_13_out), .D(Entrada[1]), .Q(d_ff_77_q));  // open: Qn, preset, en, reset
  and and_93 (and_93_out, d_ff_77_q, and_5_out);
  D_Flip_Flop d_ff_78 (.clk(and_14_out), .D(Entrada[1]), .Q(d_ff_78_q));  // open: Qn, preset, en, reset
  and and_94 (and_94_out, d_ff_78_q, and_6_out);
  D_Flip_Flop d_ff_79 (.clk(and_15_out), .D(Entrada[1]), .Q(d_ff_79_q));  // open: Qn, preset, en, reset
  and and_95 (and_95_out, d_ff_79_q, and_7_out);
  D_Flip_Flop d_ff_80 (.clk(and_16_out), .D(Entrada[1]), .Q(d_ff_80_q));  // open: Qn, preset, en, reset
  and and_96 (and_96_out, d_ff_80_q, and_8_out);
  or or_10 (out_4[1], and_96_out, and_95_out, and_94_out, and_93_out, and_92_out, and_91_out, and_90_out, and_89_out);
  D_Flip_Flop d_ff_81 (.clk(and_9_out), .D(Entrada[0]), .Q(d_ff_81_q), .preset(undriven));  // open: Qn, en, reset
  D_Flip_Flop d_ff_82 (.clk(and_10_out), .D(Entrada[0]), .Q(d_ff_82_q));  // open: Qn, preset, en, reset
  D_Flip_Flop d_ff_83 (.clk(and_11_out), .D(Entrada[0]), .Q(d_ff_83_q));  // open: Qn, preset, en, reset
  D_Flip_Flop d_ff_84 (.clk(and_12_out), .D(Entrada[0]), .Q(d_ff_84_q));  // open: Qn, preset, en, reset
  D_Flip_Flop d_ff_85 (.clk(and_13_out), .D(Entrada[0]), .Q(d_ff_85_q));  // open: Qn, preset, en, reset
  D_Flip_Flop d_ff_86 (.clk(and_14_out), .D(Entrada[0]), .Q(d_ff_86_q));  // open: Qn, preset, en, reset
  D_Flip_Flop d_ff_87 (.clk(and_15_out), .D(Entrada[0]), .Q(d_ff_87_q));  // open: Qn, preset, en, reset
  D_Flip_Flop d_ff_88 (.clk(and_16_out), .D(Entrada[0]), .Q(d_ff_88_q));  // open: Qn, preset, en, reset
  and and_97 (and_97_out, d_ff_81_q, and_1_out);
  and and_98 (and_98_out, d_ff_82_q, and_2_out);
  and and_99 (and_99_out, d_ff_83_q, and_3_out);
  and and_100 (and_100_out, d_ff_84_q, and_4_out);
  and and_101 (and_101_out, d_ff_85_q, and_5_out);
  and and_102 (and_102_out, d_ff_86_q, and_6_out);
  and and_103 (and_103_out, d_ff_87_q, and_7_out);
  and and_104 (and_104_out, d_ff_88_q, and_8_out);
  or or_11 (out_4[0], and_104_out, and_103_out, and_102_out, and_101_out, and_100_out, and_99_out, and_98_out, and_97_out);

  // Other names for the same wires on the sheet: Saida[10:0] = out_4
endmodule

// Registrador
module registrador (
  input  [7:0] in_1,
  input  WE,
  output [7:0] out_3
);

  wire and_1_out, d_ff_1_q, d_ff_2_q, d_ff_3_q, d_ff_4_q, d_ff_5_q, d_ff_6_q, d_ff_7_q, d_ff_8_q;

  and and_1 (and_1_out, 1'b1, WE);
  D_Flip_Flop d_ff_1 (.clk(and_1_out), .D(in_1[7]), .Q(d_ff_1_q));  // open: Qn, preset, en, reset
  and and_2 (out_3[7], d_ff_1_q, 1'b1);
  D_Flip_Flop d_ff_2 (.clk(and_1_out), .D(in_1[6]), .Q(d_ff_2_q));  // open: Qn, preset, en, reset
  and and_3 (out_3[6], d_ff_2_q, 1'b1);
  D_Flip_Flop d_ff_3 (.clk(and_1_out), .D(in_1[5]), .Q(d_ff_3_q));  // open: Qn, preset, en, reset
  and and_4 (out_3[5], d_ff_3_q, 1'b1);
  D_Flip_Flop d_ff_4 (.clk(and_1_out), .D(in_1[4]), .Q(d_ff_4_q));  // open: Qn, preset, en, reset
  and and_5 (out_3[4], d_ff_4_q, 1'b1);
  D_Flip_Flop d_ff_5 (.clk(and_1_out), .D(in_1[3]), .Q(d_ff_5_q));  // open: Qn, preset, en, reset
  and and_6 (out_3[3], d_ff_5_q, 1'b1);
  D_Flip_Flop d_ff_6 (.clk(and_1_out), .D(in_1[2]), .Q(d_ff_6_q));  // open: Qn, preset, en, reset
  and and_7 (out_3[2], d_ff_6_q, 1'b1);
  D_Flip_Flop d_ff_7 (.clk(and_1_out), .D(in_1[1]), .Q(d_ff_7_q));  // open: Qn, preset, en, reset
  and and_8 (out_3[1], d_ff_7_q, 1'b1);
  D_Flip_Flop d_ff_8 (.clk(and_1_out), .D(in_1[0]), .Q(d_ff_8_q));  // open: Qn, preset, en, reset
  and and_9 (out_3[0], d_ff_8_q, 1'b1);
endmodule

module soma (
  input  A,
  input  B,
  input  C,
  output S
);

  wire xor_1_out;

  xor xor_1 (xor_1_out, B, A);
  xor xor_2 (S, C, xor_1_out);
endmodule

module lookahead (
  input  [7:0] A,
  input  [7:0] B,
  input  Op,
  output [7:0] out_4
);

  wire and_1_out, and_2_out, and_3_out, and_4_out, and_5_out, and_6_out, and_7_out, and_8_out, and_9_out,
       and_10_out, and_11_out, and_12_out, and_13_out, and_14_out, and_15_out, and_16_out, and_17_out,
       and_18_out, and_19_out, and_20_out, and_21_out, and_22_out, and_23_out, and_24_out, and_25_out,
       and_26_out, and_27_out, and_28_out, and_29_out, and_30_out, and_31_out, and_32_out, and_33_out,
       and_34_out, and_35_out, and_36_out, B0, B1, B2, B3, B4, B5, B6, B7, G0, G1, G2, G3, G4, G5, G6, G7,
       or_1_out, or_2_out, or_3_out, or_4_out, or_5_out, or_6_out, or_7_out, or_8_out, P0, P1, P2, P3, P4,
       P5, P6, P7;
  wire [7:0] distribuidor_1_out_2;

  and and_1 (and_1_out, G6, P7);
  // Probe on A
  // Probe on B
  distribuidor distribuidor_1 (.in_1(Op), .out_2(distribuidor_1_out_2));
  // Probe on out_4
  and and_2 (and_2_out, G5, P6, P7);
  assign {B7, B6, B5, B4, B3, B2, B1, B0} = B ^ distribuidor_1_out_2;  // XOR_Gate xor_1, 8 bits wide
  and and_3 (and_3_out, G4, P5, P6, P7);
  or or_1 (or_1_out, and_1_out, and_2_out, and_3_out, and_4_out, and_5_out, and_7_out, and_8_out, and_6_out);
  and and_4 (and_4_out, G3, P4, P5, P6, P7);
  and and_5 (and_5_out, G2, P3, P4, P5, P6, P7);
  and and_6 (and_6_out, P7, P6, P5, P4, P3, P2, P1, P0, Op);
  and and_7 (and_7_out, G1, P2, P3, P4, P5, P6, P7);
  and and_8 (and_8_out, G0, P1, P2, P3, P4, P5, P6, P7);
  or u_P7 (P7, B7, A[7]);
  soma soma_1 (.S(out_4[7]), .A(A[7]), .B(B7), .C(or_2_out));
  and u_G7 (G7, A[7], B7);
  and and_9 (and_9_out, G4, P5, P6);
  and and_10 (and_10_out, G5, P6);
  and and_11 (and_11_out, G3, P4, P5, P6);
  or or_2 (or_2_out, G6, and_10_out, and_9_out, and_11_out, and_12_out, and_13_out, and_14_out, and_15_out);
  and and_12 (and_12_out, G2, P3, P5, P6);
  and and_13 (and_13_out, G1, P2, P3, P4, P5, P6);
  and and_14 (and_14_out, G0, P1, P2, P3, P4, P5, P6);
  and and_15 (and_15_out, P6, P5, P4, P3, P2, P1, P0, Op);
  xor u_P6 (P6, B6, A[6]);
  soma soma_2 (.S(out_4[6]), .A(A[6]), .B(B6), .C(or_3_out));
  and u_G6 (G6, A[6], B6);
  and and_16 (and_16_out, G4, P5);
  and and_17 (and_17_out, G3, P4, P5);
  or or_3 (or_3_out, G5, and_16_out, and_17_out, and_18_out, and_19_out, and_20_out, and_21_out);
  and and_18 (and_18_out, G2, P3, P4, P5);
  and and_19 (and_19_out, G1, P2, P3, P4, P5);
  and and_20 (and_20_out, G0, P1, P2, P3, P4, P5);
  and and_21 (and_21_out, P5, P4, P3, P2, P1, P0, Op);
  xor u_P5 (P5, B5, A[5]);
  and u_G5 (G5, A[5], B5);
  and and_22 (and_22_out, G3, P4);
  soma soma_3 (.S(out_4[5]), .A(A[5]), .B(B5), .C(or_4_out));
  and and_23 (and_23_out, G2, P3, P4);
  or or_4 (or_4_out, G4, and_22_out, and_23_out, and_24_out, and_25_out, and_26_out);
  and and_24 (and_24_out, G1, P2, P3, P4);
  and and_25 (and_25_out, G0, P1, P2, P3, P4);
  and u_G4 (G4, A[4], B4);
  and and_26 (and_26_out, P4, P3, P2, P1, P0, Op);
  xor u_P4 (P4, A[4], B4);
  and and_27 (and_27_out, G2, P3);
  or or_5 (or_5_out, G3, and_27_out, and_28_out, and_29_out, and_30_out);
  soma soma_4 (.S(out_4[4]), .A(A[4]), .B(B4), .C(or_5_out));
  and and_28 (and_28_out, G1, P2, P3);
  and and_29 (and_29_out, G0, P1, P2, P3);
  and u_G3 (G3, A[3], B3);
  xor u_P3 (P3, A[3], B3);
  and and_30 (and_30_out, P3, P2, P1, P0, Op);
  soma soma_5 (.S(out_4[3]), .A(A[3]), .B(B3), .C(or_6_out));
  xor P3_2 (P2, A[2], B2);
  and and_31 (and_31_out, G0, P1, P2);
  and and_32 (and_32_out, G1, P2);
  or or_6 (or_6_out, G2, and_32_out, and_31_out, and_33_out);
  and u_G2 (G2, A[2], B2);
  and and_33 (and_33_out, P2, P1, P0, Op);
  and and_34 (and_34_out, G0, P1);
  or or_7 (or_7_out, G1, and_34_out, and_35_out);
  soma soma_6 (.S(out_4[2]), .A(A[2]), .B(B2), .C(or_7_out));
  and u_G1 (G1, A[1], B1);
  and and_35 (and_35_out, P1, P0, Op);
  and u_G0 (G0, A[0], B0);
  xor u_P1 (P1, A[1], B1);
  and and_36 (and_36_out, P0, Op);
  or or_8 (or_8_out, G0, and_36_out);
  soma soma_7 (.S(out_4[1]), .A(A[1]), .B(B1), .C(or_8_out));
  xor u_P0 (P0, A[0], B0);
  soma soma_8 (.S(out_4[0]), .A(A[0]), .B(B0), .C(Op));

  // Other names for the same wires on the sheet: RES[7:0] = out_4
endmodule

module distribuidor (
  input  in_1,
  output [7:0] out_2
);


  assign out_2 = {8{in_1}};
endmodule

module ULA (
  input  [7:0] A,
  input  [7:0] B,
  input  [2:0] in_3,
  output [7:0] out_4
);

  wire tunnel;
  wire [7:0] and_1_out, divider_1_out, divider_1_rem, lookahead_1_out_4, multiplier_1_out, or_1_out,
       xor_1_out;

  // Probe on A
  // Probe on B
  assign xor_1_out = B ^ A;  // XOR_Gate xor_1, 8 bits wide
  lookahead lookahead_1 (.A(A), .B(B), .Op(tunnel), .out_4(lookahead_1_out_4));
  Multiplier multiplier_1 (.a(B), .b(A), .out(multiplier_1_out));  // open: cin, cout
  Divider divider_1 (.a(A), .b(B), .out(divider_1_out), .rem(divider_1_rem));  // open: upper
  assign and_1_out = B & A;  // AND_Gate and_1, 8 bits wide
  assign or_1_out = B | A;  // OR_Gate or_1, 8 bits wide
  Multiplexer #(.select(3), .width(8)) multiplexer_1 (
    .in0(and_1_out), .in1(or_1_out), .in2(xor_1_out), .in3(lookahead_1_out_4), .in4(lookahead_1_out_4),
    .in5(multiplier_1_out), .in6(divider_1_out), .in7(divider_1_rem), .out(out_4), .sel(in_3));  // open: en
  // Probe on out_4
  and and_2 (tunnel, ~in_3[0], ~in_3[1], in_3[2]);  // AND_Gate
endmodule

module contador (
  input  in_1,
  output R_W,
  output [2:0] Num
);

  wire undriven;

  T_Flip_Flop #(.trigger("falling")) t_ff_1 (.clk(in_1), .T(1'b1), .Q(Num[0]));  // open: Qn, preset, reset, en
  T_Flip_Flop #(.trigger("falling")) t_ff_2 (.clk(Num[0]), .T(1'b1), .Q(Num[1]));  // open: Qn, preset, reset, en
  T_Flip_Flop #(.trigger("falling")) t_ff_3 (
    .clk(Num[1]), .T(1'b1), .Q(Num[2]), .reset(undriven));  // open: Qn, preset, en

  assign R_W = Num[0];
endmodule
