// Logisim project datapath5.circ as structural Verilog: 12 circuits, main circuit main
// ULA
module main (
  output Overflow
);

  wire _0, AluSrc, and_1_out, and_2_out, and_3_out, Bne, Branch, Ck, Jal, Jr, Jump, MemRead, MemToReg,
       MemWrite, multiplexer_2_out, not_1_out, RegDst, WriteReg;
  wire [2:0] AluOP;
  wire [3:0] Controle_ULA_op_ula;
  wire [4:0] decodificador_instrucoes_1_rd, decodificador_instrucoes_1_rs, decodificador_instrucoes_1_rt,
       decodificador_instrucoes_1_shamt, multiplexer_5_out, multiplexer_6_out;
  wire [5:0] decodificador_instrucoes_1_funct, decodificador_instrucoes_1_opcode;
  wire [15:0] decodificador_instrucoes_1_imm;
  wire [25:0] decodificador_instrucoes_1_addr;
  wire [31:0] adder_1_out, br_1_ld1, br_1_ld2, datamem_1_p6, extensor_16bits_1_out_2, meminstr_1_p2,
       multiplexer_1_out, multiplexer_3_out, multiplexer_4_out, multiplexer_7_out, multiplexer_8_out,
       multiplexer_9_out, n2conc_1_out_3, PC_4, register_1_q, shifter_1_out, ula_1_result;

  // Probe on adder_1_out
  Adder #(.width(32)) adder_1 (.a(PC_4), .b(shifter_1_out), .out(adder_1_out));  // open: cin, cout
  not not_1 (not_1_out, _0);
  Multiplexer #(.width(32), .enable("false")) multiplexer_1 (
    .in0(PC_4), .in1(adder_1_out), .out(multiplexer_1_out), .sel(and_1_out));
  and and_1 (and_1_out, multiplexer_2_out, Branch);
  Multiplexer #(.enable("false")) multiplexer_2 (.in0(_0), .in1(not_1_out), .out(multiplexer_2_out), .sel(Bne));
  // Probe on multiplexer_1_out
  Multiplexer #(.width(32), .enable("false")) multiplexer_3 (
    .in0(multiplexer_1_out), .in1(n2conc_1_out_3), .out(multiplexer_3_out), .sel(Jump));
  Shifter #(.width(32)) shifter_1 (.in(extensor_16bits_1_out_2), .\dist (5'b00010), .out(shifter_1_out));
  Multiplexer #(.width(32), .enable("false")) multiplexer_4 (
    .in0(multiplexer_3_out), .in1(br_1_ld1), .out(multiplexer_4_out), .sel(and_2_out));
  and and_2 (and_2_out, ~Jump, Jr);  // AND_Gate
  Register #(.width(32)) register_1 (.D(multiplexer_4_out), .Q(register_1_q), .clk(Ck));  // open: en, clr
  // Probe on multiplexer_4_out
  // Probe on n2conc_1_out_3
  // Probe on extensor_16bits_1_out_2
  Clock clock_1 (.out(Ck));
  _2conc u_2conc_1 (.Pc_4(PC_4), .Addr(decodificador_instrucoes_1_addr), .out_3(n2conc_1_out_3));
  // Probe on PC_4
  Adder #(.width(32)) adder_2 (.a(32'h4), .b(register_1_q), .out(PC_4));  // open: cin, cout
  // MemInstr meminstr_1: pin names not known; wires that end beside it: register_1_q, meminstr_1_p2
  // Probe on meminstr_1_p2
  decodificador_instrucoes decodificador_instrucoes_1 (
    .\Instrução (meminstr_1_p2), .imm(decodificador_instrucoes_1_imm),
    .addr(decodificador_instrucoes_1_addr), .opcode(decodificador_instrucoes_1_opcode),
    .rs(decodificador_instrucoes_1_rs), .rt(decodificador_instrucoes_1_rt),
    .rd(decodificador_instrucoes_1_rd), .shamt(decodificador_instrucoes_1_shamt),
    .funct(decodificador_instrucoes_1_funct));
  extensor_16bits extensor_16bits_1 (.in_1(decodificador_instrucoes_1_imm), .out_2(extensor_16bits_1_out_2));
  unidade_controle Unidade_Controle (
    .Opcode(decodificador_instrucoes_1_opcode), .RegDst(RegDst), .AluSrc(AluSrc), .WriteReg(WriteReg),
    .MemRead(MemRead), .MemToReg(MemToReg), .MemWrite(MemWrite), .Branch(Branch), .Bne(Bne), .Jump(Jump),
    .AluOp(AluOP), .Link(Jal));
  Multiplexer #(.width(5)) multiplexer_5 (
    .in0(decodificador_instrucoes_1_rt), .in1(decodificador_instrucoes_1_rd), .out(multiplexer_5_out),
    .sel(RegDst));  // open: en
  // Probe on multiplexer_7_out
  Multiplexer #(.width(5)) multiplexer_6 (
    .in0(multiplexer_5_out), .in1({5{1'b1}}), .out(multiplexer_6_out), .sel(Jal));  // open: en
  and and_3 (and_3_out, WriteReg, ~Jr);  // AND_Gate
  Multiplexer #(.width(32)) multiplexer_7 (
    .in0(multiplexer_9_out), .in1(PC_4), .out(multiplexer_7_out), .sel(Jal));  // open: en
  BR br_1 (
    .LD1(br_1_ld1), .LR1(decodificador_instrucoes_1_rs), .LD2(br_1_ld2), .LR2(decodificador_instrucoes_1_rt),
    .WD(multiplexer_7_out), .RegWrite(and_3_out), .WR(multiplexer_6_out), .Ck(Ck));
  controle_ULA Controle_ULA (
    .funct(decodificador_instrucoes_1_funct), .Op_ULA(Controle_ULA_op_ula), .AluOp(AluOP), .Jr(Jr));
  // Probe on br_1_ld1
  // Probe on multiplexer_8_out
  Multiplexer #(.width(32)) multiplexer_8 (
    .in0(br_1_ld2), .in1(extensor_16bits_1_out_2), .out(multiplexer_8_out), .sel(AluSrc));  // open: en
  ULA ula_1 (
    .OpALU(Controle_ULA_op_ula), .Result(ula_1_result), .A(br_1_ld1),
    .Shamt(decodificador_instrucoes_1_shamt), .B(multiplexer_8_out), .out_5(_0), .Overflow(Overflow));
  // Probe on ula_1_result
  // datamem datamem_1: pin names not known; wires that end beside it: ula_1_result, br_1_ld2, MemRead, MemWrite, Ck, datamem_1_p6
  Multiplexer #(.width(32), .enable("false")) multiplexer_9 (
    .in0(ula_1_result), .in1(datamem_1_p6), .out(multiplexer_9_out), .sel(MemToReg));

  // Notes on the sheet:
  //   LD1
  //   PC
  //   PC + 4
  //   opcode
  //   rs
  //   rt
  //   rd
  //   shamt
  //   funct
  //   imm
  //   addr
  //   Extensor
  //   Jr
  //   funct
  //   OpAlu
  //   OpAlu
  //   Shamt
endmodule

module ULA (
  input  [31:0] A,
  input  [31:0] B,
  input  [4:0] Shamt,
  input  [3:0] OpALU,
  output out_5,
  output [31:0] Result,
  output Overflow
);

  wire and_2_out, and_3_out, and_4_out, and_5_out, comparator_1_lt, overflow_add_overflow,
       overflow_sub_overflow;
  wire [31:0] adder_1_out, and_1_out, extensor_1_out_2, nor_1_out, or_1_out, shifter_1_out, shifter_2_out,
       subtractor_1_out, xor_1_out;

  // Probe on A
  // Probe on B
  assign and_1_out = A & B;  // AND_Gate and_1, 32 bits wide
  assign or_1_out = A | B;  // OR_Gate or_1, 32 bits wide
  assign nor_1_out = ~(A | B);  // NOR_Gate nor_1, 32 bits wide
  assign xor_1_out = A ^ B;  // XOR_Gate xor_1, 32 bits wide
  Comparator #(.width(32)) comparator_1 (.a(A), .b(B), .lt(comparator_1_lt));  // open: gt, eq
  Adder #(.width(32)) adder_1 (.a(A), .b(B), .out(adder_1_out));  // open: cin, cout
  Subtractor #(.width(32)) subtractor_1 (.a(A), .b(B), .out(subtractor_1_out));  // open: bin, bout
  Shifter #(.width(32)) shifter_1 (.in(B), .\dist (Shamt), .out(shifter_1_out));
  Shifter #(.width(32), .shift("lr")) shifter_2 (.in(B), .\dist (Shamt), .out(shifter_2_out));
  extensor extensor_1 (.in_1(comparator_1_lt), .out_2(extensor_1_out_2));
  overflow_sub overflow_sub (.a(A), .b(B), .res(subtractor_1_out), .overflow(overflow_sub_overflow));
  // Probe on extensor_1_out_2
  overflow overflow_add (.overflow(overflow_add_overflow), .a(A), .res(adder_1_out), .b(B));
  Multiplexer #(.select(4), .width(32)) multiplexer_1 (
    .in0(and_1_out), .in1(or_1_out), .in2(nor_1_out), .in3(xor_1_out), .in4(extensor_1_out_2),
    .in5(adder_1_out), .in6(subtractor_1_out), .in7(shifter_1_out), .in8(shifter_2_out), .out(Result),
    .sel(OpALU));  // open: in9, in10, in11, in12, in13, in14, in15, en
  pega_zero pega_zero_1 (.in_1(Result), .out_2(out_5));
  // Probe on OpALU
  and and_2 (and_2_out, OpALU[0], ~OpALU[1], OpALU[2], ~OpALU[3]);  // AND_Gate
  and and_3 (and_3_out, and_2_out, overflow_add_overflow);
  and and_4 (and_4_out, overflow_sub_overflow, and_5_out);
  and and_5 (and_5_out, ~OpALU[0], OpALU[1], OpALU[2], ~OpALU[3]);  // AND_Gate
  or or_2 (Overflow, and_3_out, and_4_out);
  // Probe on Result

  // Notes on the sheet:
  //   OpAlu
  //   0000 - AND
  //   0001 - OR
  //   0010 - NOR
  //   0011 - XOR
  //   0100 - SLT
  //   0101 - ADD
  //   0110 - SUB
  //   0111 - SLL
  //   1000 - SRL
endmodule

module BR (
  input  Ck,
  input  [31:0] WD,
  input  RegWrite,
  input  [4:0] LR1,
  input  [4:0] WR,
  input  [4:0] LR2,
  output [31:0] LD1,
  output [31:0] LD2
);

  wire demultiplexer_1_out0, demultiplexer_1_out1, demultiplexer_1_out2, demultiplexer_1_out3,
       demultiplexer_1_out4, demultiplexer_1_out5, demultiplexer_1_out6, demultiplexer_1_out7,
       demultiplexer_1_out8, demultiplexer_1_out9, demultiplexer_1_out10, demultiplexer_1_out11,
       demultiplexer_1_out12, demultiplexer_1_out13, demultiplexer_1_out14, demultiplexer_1_out15,
       demultiplexer_1_out16, demultiplexer_1_out17, demultiplexer_1_out18, demultiplexer_1_out19,
       demultiplexer_1_out20, demultiplexer_1_out21, demultiplexer_1_out22, demultiplexer_1_out23,
       demultiplexer_1_out24, demultiplexer_1_out25, demultiplexer_1_out26, demultiplexer_1_out27,
       demultiplexer_1_out28, demultiplexer_1_out29, demultiplexer_1_out30, demultiplexer_1_out31,
       demultiplexer_2_out0, demultiplexer_2_out1, demultiplexer_2_out2, demultiplexer_2_out3,
       demultiplexer_2_out4, demultiplexer_2_out5, demultiplexer_2_out6, demultiplexer_2_out7,
       demultiplexer_2_out8, demultiplexer_2_out9, demultiplexer_2_out10, demultiplexer_2_out11,
       demultiplexer_2_out12, demultiplexer_2_out13, demultiplexer_2_out14, demultiplexer_2_out15,
       demultiplexer_2_out16, demultiplexer_2_out17, demultiplexer_2_out18, demultiplexer_2_out19,
       demultiplexer_2_out20, demultiplexer_2_out21, demultiplexer_2_out22, demultiplexer_2_out23,
       demultiplexer_2_out24, demultiplexer_2_out25, demultiplexer_2_out26, demultiplexer_2_out27,
       demultiplexer_2_out28, demultiplexer_2_out29, demultiplexer_2_out30, demultiplexer_2_out31;
  wire [31:0] _00000_2_q, _00000_q, _00001_2_q, _00001_q, _00010_2_q, _00010_q, _00011_2_q, _00011_q,
       _00100_2_q, _00100_q, _00101_2_q, _00101_q, _00110_2_q, _00110_q, _00111_2_q, _00111_q, _01000_2_q,
       _01000_q, _01001_2_q, _01001_q, _01010_2_q, _01010_q, _01011_2_q, _01011_q, _01100_2_q, _01100_q,
       _01101_2_q, _01101_q, _01110_2_q, _01110_q, _01111_2_q, _01111_q, _10000_2_q, _10000_q, _10001_2_q,
       _10001_q, _10010_2_q, _10010_q, _10011_2_q, _10011_q, _10100_2_q, _10100_q, _10101_2_q, _10101_q,
       _10110_2_q, _10110_q, _10111_2_q, _10111_q, _11000_2_q, _11000_q, _11001_2_q, _11001_q, _11010_2_q,
       _11010_q, _11011_2_q, _11011_q, _11100_2_q, _11100_q, _11101_2_q, _11101_q, _11110_2_q, _11110_q,
       _11111_2_q, _11111_q, and_1_out, and_2_out;

  // Probe on WD
  Demultiplexer #(.select(5)) demultiplexer_1 (
    .out0(demultiplexer_1_out0), .out1(demultiplexer_1_out1), .out2(demultiplexer_1_out2),
    .out3(demultiplexer_1_out3), .out4(demultiplexer_1_out4), .out5(demultiplexer_1_out5),
    .out6(demultiplexer_1_out6), .out7(demultiplexer_1_out7), .out8(demultiplexer_1_out8),
    .out9(demultiplexer_1_out9), .out10(demultiplexer_1_out10), .out11(demultiplexer_1_out11),
    .out12(demultiplexer_1_out12), .out13(demultiplexer_1_out13), .out14(demultiplexer_1_out14),
    .out15(demultiplexer_1_out15), .out16(demultiplexer_1_out16), .out17(demultiplexer_1_out17),
    .out18(demultiplexer_1_out18), .out19(demultiplexer_1_out19), .out20(demultiplexer_1_out20),
    .out21(demultiplexer_1_out21), .out22(demultiplexer_1_out22), .out23(demultiplexer_1_out23),
    .out24(demultiplexer_1_out24), .out25(demultiplexer_1_out25), .out26(demultiplexer_1_out26),
    .out27(demultiplexer_1_out27), .out28(demultiplexer_1_out28), .out29(demultiplexer_1_out29),
    .out30(demultiplexer_1_out30), .out31(demultiplexer_1_out31), .in(RegWrite), .sel(WR));  // open: en
  // Probe on WR
  Demultiplexer #(.select(5)) demultiplexer_2 (
    .out0(demultiplexer_2_out0), .out1(demultiplexer_2_out1), .out2(demultiplexer_2_out2),
    .out3(demultiplexer_2_out3), .out4(demultiplexer_2_out4), .out5(demultiplexer_2_out5),
    .out6(demultiplexer_2_out6), .out7(demultiplexer_2_out7), .out8(demultiplexer_2_out8),
    .out9(demultiplexer_2_out9), .out10(demultiplexer_2_out10), .out11(demultiplexer_2_out11),
    .out12(demultiplexer_2_out12), .out13(demultiplexer_2_out13), .out14(demultiplexer_2_out14),
    .out15(demultiplexer_2_out15), .out16(demultiplexer_2_out16), .out17(demultiplexer_2_out17),
    .out18(demultiplexer_2_out18), .out19(demultiplexer_2_out19), .out20(demultiplexer_2_out20),
    .out21(demultiplexer_2_out21), .out22(demultiplexer_2_out22), .out23(demultiplexer_2_out23),
    .out24(demultiplexer_2_out24), .out25(demultiplexer_2_out25), .out26(demultiplexer_2_out26),
    .out27(demultiplexer_2_out27), .out28(demultiplexer_2_out28), .out29(demultiplexer_2_out29),
    .out30(demultiplexer_2_out30), .out31(demultiplexer_2_out31), .in(RegWrite), .sel(WR));  // open: en
  // Probe on WR
  Register #(.width(32)) _00000 (.D(WD), .en(demultiplexer_1_out0), .Q(_00000_q), .clk(Ck));  // open: clr
  Register #(.width(32)) _00001 (.D(WD), .en(demultiplexer_1_out1), .Q(_00001_q), .clk(Ck));  // open: clr
  Register #(.width(32)) _00010 (.D(WD), .en(demultiplexer_1_out2), .Q(_00010_q), .clk(Ck));  // open: clr
  Register #(.width(32)) _00011 (.D(WD), .en(demultiplexer_1_out3), .Q(_00011_q), .clk(Ck));  // open: clr
  Register #(.width(32)) _00100 (.D(WD), .en(demultiplexer_1_out4), .Q(_00100_q), .clk(Ck));  // open: clr
  Register #(.width(32)) _00101 (.D(WD), .en(demultiplexer_1_out5), .Q(_00101_q), .clk(Ck));  // open: clr
  Register #(.width(32)) _00110 (.D(WD), .en(demultiplexer_1_out6), .Q(_00110_q), .clk(Ck));  // open: clr
  Register #(.width(32)) _00111 (.D(WD), .en(demultiplexer_1_out7), .Q(_00111_q), .clk(Ck));  // open: clr
  Register #(.width(32)) _01000 (.D(WD), .en(demultiplexer_1_out8), .Q(_01000_q), .clk(Ck));  // open: clr
  Register #(.width(32)) _01001 (.D(WD), .en(demultiplexer_1_out9), .Q(_01001_q), .clk(Ck));  // open: clr
  Register #(.width(32)) _01010 (.D(WD), .en(demultiplexer_1_out10), .Q(_01010_q), .clk(Ck));  // open: clr
  Register #(.width(32)) _01011 (.D(WD), .en(demultiplexer_1_out11), .Q(_01011_q), .clk(Ck));  // open: clr
  Register #(.width(32)) _01100 (.D(WD), .en(demultiplexer_1_out12), .Q(_01100_q), .clk(Ck));  // open: clr
  Register #(.width(32)) _01101 (.D(WD), .en(demultiplexer_1_out13), .Q(_01101_q), .clk(Ck));  // open: clr
  Register #(.width(32)) _01110 (.D(WD), .en(demultiplexer_1_out14), .Q(_01110_q), .clk(Ck));  // open: clr
  Register #(.width(32)) _01111 (.D(WD), .en(demultiplexer_1_out15), .Q(_01111_q), .clk(Ck));  // open: clr
  Register #(.width(32)) _10000 (.D(WD), .en(demultiplexer_1_out16), .Q(_10000_q), .clk(Ck));  // open: clr
  Register #(.width(32)) _10001 (.D(WD), .en(demultiplexer_1_out17), .Q(_10001_q), .clk(Ck));  // open: clr
  Register #(.width(32)) _10010 (.D(WD), .en(demultiplexer_1_out18), .Q(_10010_q), .clk(Ck));  // open: clr
  Register #(.width(32)) _10011 (.D(WD), .en(demultiplexer_1_out19), .Q(_10011_q), .clk(Ck));  // open: clr
  Register #(.width(32)) _10100 (.D(WD), .en(demultiplexer_1_out20), .Q(_10100_q), .clk(Ck));  // open: clr
  Register #(.width(32)) _10101 (.D(WD), .en(demultiplexer_1_out21), .Q(_10101_q), .clk(Ck));  // open: clr
  Register #(.width(32)) _10110 (.D(WD), .en(demultiplexer_1_out22), .Q(_10110_q), .clk(Ck));  // open: clr
  Register #(.width(32)) _10111 (.D(WD), .en(demultiplexer_1_out23), .Q(_10111_q), .clk(Ck));  // open: clr
  Register #(.width(32)) _11000 (.D(WD), .en(demultiplexer_1_out24), .Q(_11000_q), .clk(Ck));  // open: clr
  Register #(.width(32)) _11001 (.D(WD), .en(demultiplexer_1_out25), .Q(_11001_q), .clk(Ck));  // open: clr
  Register #(.width(32)) _11010 (.D(WD), .en(demultiplexer_1_out26), .Q(_11010_q), .clk(Ck));  // open: clr
  Register #(.width(32)) _11011 (.D(WD), .en(demultiplexer_1_out27), .Q(_11011_q), .clk(Ck));  // open: clr
  Register #(.width(32)) _11100 (.D(WD), .en(demultiplexer_1_out28), .Q(_11100_q), .clk(Ck));  // open: clr
  Register #(.width(32)) _11101 (.D(WD), .en(demultiplexer_1_out29), .Q(_11101_q), .clk(Ck));  // open: clr
  Register #(.width(32)) _11110 (.D(WD), .en(demultiplexer_1_out30), .Q(_11110_q), .clk(Ck));  // open: clr
  Register #(.width(32)) _11111 (.D(WD), .en(demultiplexer_1_out31), .Q(_11111_q), .clk(Ck));  // open: clr
  Register #(.width(32)) _00000_2 (.D(WD), .en(demultiplexer_2_out0), .Q(_00000_2_q), .clk(Ck));  // open: clr
  Register #(.width(32)) _00001_2 (.D(WD), .en(demultiplexer_2_out1), .Q(_00001_2_q), .clk(Ck));  // open: clr
  Register #(.width(32)) _00010_2 (.D(WD), .en(demultiplexer_2_out2), .Q(_00010_2_q), .clk(Ck));  // open: clr
  Register #(.width(32)) _00011_2 (.D(WD), .en(demultiplexer_2_out3), .Q(_00011_2_q), .clk(Ck));  // open: clr
  Register #(.width(32)) _00100_2 (.D(WD), .en(demultiplexer_2_out4), .Q(_00100_2_q), .clk(Ck));  // open: clr
  Register #(.width(32)) _00101_2 (.D(WD), .en(demultiplexer_2_out5), .Q(_00101_2_q), .clk(Ck));  // open: clr
  Register #(.width(32)) _00110_2 (.D(WD), .en(demultiplexer_2_out6), .Q(_00110_2_q), .clk(Ck));  // open: clr
  Register #(.width(32)) _00111_2 (.D(WD), .en(demultiplexer_2_out7), .Q(_00111_2_q), .clk(Ck));  // open: clr
  Register #(.width(32)) _01000_2 (.D(WD), .en(demultiplexer_2_out8), .Q(_01000_2_q), .clk(Ck));  // open: clr
  Register #(.width(32)) _01001_2 (.D(WD), .en(demultiplexer_2_out9), .Q(_01001_2_q), .clk(Ck));  // open: clr
  Register #(.width(32)) _01010_2 (.D(WD), .en(demultiplexer_2_out10), .Q(_01010_2_q), .clk(Ck));  // open: clr
  Register #(.width(32)) _01011_2 (.D(WD), .en(demultiplexer_2_out11), .Q(_01011_2_q), .clk(Ck));  // open: clr
  Register #(.width(32)) _01100_2 (.D(WD), .en(demultiplexer_2_out12), .Q(_01100_2_q), .clk(Ck));  // open: clr
  Register #(.width(32)) _01101_2 (.D(WD), .en(demultiplexer_2_out13), .Q(_01101_2_q), .clk(Ck));  // open: clr
  Register #(.width(32)) _01110_2 (.D(WD), .en(demultiplexer_2_out14), .Q(_01110_2_q), .clk(Ck));  // open: clr
  Register #(.width(32)) _01111_2 (.D(WD), .en(demultiplexer_2_out15), .Q(_01111_2_q), .clk(Ck));  // open: clr
  Register #(.width(32)) _10000_2 (.D(WD), .en(demultiplexer_2_out16), .Q(_10000_2_q), .clk(Ck));  // open: clr
  Register #(.width(32)) _10001_2 (.D(WD), .en(demultiplexer_2_out17), .Q(_10001_2_q), .clk(Ck));  // open: clr
  Register #(.width(32)) _10010_2 (.D(WD), .en(demultiplexer_2_out18), .Q(_10010_2_q), .clk(Ck));  // open: clr
  Register #(.width(32)) _10011_2 (.D(WD), .en(demultiplexer_2_out19), .Q(_10011_2_q), .clk(Ck));  // open: clr
  Register #(.width(32)) _10100_2 (.D(WD), .en(demultiplexer_2_out20), .Q(_10100_2_q), .clk(Ck));  // open: clr
  Register #(.width(32)) _10101_2 (.D(WD), .en(demultiplexer_2_out21), .Q(_10101_2_q), .clk(Ck));  // open: clr
  Register #(.width(32)) _10110_2 (.D(WD), .en(demultiplexer_2_out22), .Q(_10110_2_q), .clk(Ck));  // open: clr
  Register #(.width(32)) _10111_2 (.D(WD), .en(demultiplexer_2_out23), .Q(_10111_2_q), .clk(Ck));  // open: clr
  Register #(.width(32)) _11000_2 (.D(WD), .en(demultiplexer_2_out24), .Q(_11000_2_q), .clk(Ck));  // open: clr
  Register #(.width(32)) _11001_2 (.D(WD), .en(demultiplexer_2_out25), .Q(_11001_2_q), .clk(Ck));  // open: clr
  Register #(.width(32)) _11010_2 (.D(WD), .en(demultiplexer_2_out26), .Q(_11010_2_q), .clk(Ck));  // open: clr
  Register #(.width(32)) _11011_2 (.D(WD), .en(demultiplexer_2_out27), .Q(_11011_2_q), .clk(Ck));  // open: clr
  Register #(.width(32)) _11100_2 (.D(WD), .en(demultiplexer_2_out28), .Q(_11100_2_q), .clk(Ck));  // open: clr
  Register #(.width(32)) _11101_2 (.D(WD), .en(demultiplexer_2_out29), .Q(_11101_2_q), .clk(Ck));  // open: clr
  Register #(.width(32)) _11110_2 (.D(WD), .en(demultiplexer_2_out30), .Q(_11110_2_q), .clk(Ck));  // open: clr
  Register #(.width(32)) _11111_2 (.D(WD), .en(demultiplexer_2_out31), .Q(_11111_2_q), .clk(Ck));  // open: clr
  assign and_1_out = {32{1'b0}} & _00000_q;  // AND_Gate and_1, 32 bits wide
  assign and_2_out = {32{1'b0}} & _00000_2_q;  // AND_Gate and_2, 32 bits wide
  Multiplexer #(.select(5), .width(32)) multiplexer_1 (
    .in0(and_1_out), .in1(_00001_q), .in2(_00010_q), .in3(_00011_q), .in4(_00100_q), .in5(_00101_q),
    .in6(_00110_q), .in7(_00111_q), .in8(_01000_q), .in9(_01001_q), .in10(_01010_q), .in11(_01011_q),
    .in12(_01100_q), .in13(_01101_q), .in14(_01110_q), .in15(_01111_q), .in16(_10000_q), .in17(_10001_q),
    .in18(_10010_q), .in19(_10011_q), .in20(_10100_q), .in21(_10101_q), .in22(_10110_q), .in23(_10111_q),
    .in24(_11000_q), .in25(_11001_q), .in26(_11010_q), .in27(_11011_q), .in28(_11100_q), .in29(_11101_q),
    .in30(_11110_q), .in31(_11111_q), .out(LD1), .sel(LR1));  // open: en
  Multiplexer #(.select(5), .width(32)) multiplexer_2 (
    .in0(and_2_out), .in1(_00001_2_q), .in2(_00010_2_q), .in3(_00011_2_q), .in4(_00100_2_q),
    .in5(_00101_2_q), .in6(_00110_2_q), .in7(_00111_2_q), .in8(_01000_2_q), .in9(_01001_2_q),
    .in10(_01010_2_q), .in11(_01011_2_q), .in12(_01100_2_q), .in13(_01101_2_q), .in14(_01110_2_q),
    .in15(_01111_2_q), .in16(_10000_2_q), .in17(_10001_2_q), .in18(_10010_2_q), .in19(_10011_2_q),
    .in20(_10100_2_q), .in21(_10101_2_q), .in22(_10110_2_q), .in23(_10111_2_q), .in24(_11000_2_q),
    .in25(_11001_2_q), .in26(_11010_2_q), .in27(_11011_2_q), .in28(_11100_2_q), .in29(_11101_2_q),
    .in30(_11110_2_q), .in31(_11111_2_q), .out(LD2), .sel(LR2));  // open: en
  // Probe on LD1
  // Probe on LR1
  // Probe on LD2
  // Probe on LR2

  // Notes on the sheet:
  //   $0
  //   $1
  //   $2-$3
  //   $4–$7
  //   $8–$15
  //   $16–$23
  //   $24–$25
  //   $26–$27
  //   $28
  //   $29
  //   $30
  //   $31
  //   $0
  //   $1
  //   $2-$3
  //   $4–$7
  //   $8–$15
  //   $16–$23
  //   $24–$25
  //   $26–$27
  //   $28
  //   $29
  //   $30
  //   $31
  //   Registradores
  //   $zero
  //   $at
  //   $v0-$v1
  //   $a0–$a3
  //   $t0–$t7
  //   $s0–$s7
  //   $t8–$t9
  //   $k0–$k1
  //   $gp
  //   $sp
  //   $fp
  //   $ra
  //   Registradores
  //   $zero
  //   $at
  //   $v0-$v1
  //   $a0–$a3
  //   $t0–$t7
  //   $s0–$s7
  //   $t8–$t9
  //   $k0–$k1
  //   $gp
  //   $sp
  //   $fp
  //   $ra
endmodule

module pega_zero (
  input  [31:0] in_1,
  output out_2
);

  nor nor_1 (out_2, in_1[0], in_1[1], in_1[2], in_1[3], in_1[4], in_1[5], in_1[6], in_1[7], in_1[8], in_1[9], in_1[10], in_1[11], in_1[12], in_1[13], in_1[14], in_1[15], in_1[16], in_1[17], in_1[18], in_1[19], in_1[20], in_1[21], in_1[22], in_1[23], in_1[24], in_1[25], in_1[26], in_1[27], in_1[28], in_1[29], in_1[30], in_1[31]);
endmodule

module extensor (
  input  in_1,
  output [31:0] out_2
);


  assign out_2 = {32{in_1}};
endmodule

module overflow (
  input  [31:0] a,
  input  [31:0] b,
  input  [31:0] res,
  output overflow
);

  wire and_1_out, and_2_out, not_1_out, not_2_out, not_3_out;

  not not_1 (not_1_out, a[31]);
  not not_2 (not_2_out, b[31]);
  not not_3 (not_3_out, res[31]);
  and and_1 (and_1_out, not_1_out, not_2_out, res[31]);
  and and_2 (and_2_out, a[31], b[31], not_3_out);
  or or_1 (overflow, and_1_out, and_2_out);
endmodule

module overflow_sub (
  input  [31:0] a,
  input  [31:0] b,
  input  [31:0] res,
  output overflow
);

  wire and_1_out, and_2_out, not_1_out, not_2_out, not_3_out;

  not not_1 (not_1_out, a[31]);
  not not_2 (not_2_out, b[31]);
  not not_3 (not_3_out, res[31]);
  and and_1 (and_1_out, not_1_out, b[31], res[31]);
  and and_2 (and_2_out, a[31], not_2_out, not_3_out);
  or or_1 (overflow, and_1_out, and_2_out);
endmodule

module unidade_controle (
  input  [5:0] Opcode,
  output RegDst,
  output WriteReg,
  output AluSrc,
  output MemRead,
  output MemToReg,
  output MemWrite,
  output Branch,
  output Bne,
  output Jump,
  output Link,
  output [2:0] AluOp
);

  wire addi_out, andi_out, beq_out, j_out, ori_out;

  nor R (RegDst, Opcode[0], Opcode[1], Opcode[2], Opcode[3], Opcode[4], Opcode[5]);
  and lw (MemRead, Opcode[0], Opcode[1], ~Opcode[2], ~Opcode[3], ~Opcode[4], Opcode[5]);  // AND_Gate
  and sw (MemWrite, Opcode[0], Opcode[1], ~Opcode[2], Opcode[3], ~Opcode[4], Opcode[5]);  // AND_Gate
  and beq (beq_out, ~Opcode[0], ~Opcode[1], Opcode[2], ~Opcode[3], ~Opcode[4], ~Opcode[5]);  // AND_Gate
  and addi (addi_out, ~Opcode[0], ~Opcode[1], ~Opcode[2], Opcode[3], ~Opcode[4], ~Opcode[5]);  // AND_Gate
  and u_bne (Bne, Opcode[0], ~Opcode[1], Opcode[2], ~Opcode[3], ~Opcode[4], ~Opcode[5]);  // AND_Gate
  and j (j_out, ~Opcode[0], Opcode[1], ~Opcode[2], ~Opcode[3], ~Opcode[4], ~Opcode[5]);  // AND_Gate
  and jal (Link, Opcode[0], Opcode[1], ~Opcode[2], ~Opcode[3], ~Opcode[4], ~Opcode[5]);  // AND_Gate
  and ori (ori_out, Opcode[0], ~Opcode[1], Opcode[2], Opcode[3], ~Opcode[4], ~Opcode[5]);  // AND_Gate
  and andi (andi_out, ~Opcode[0], ~Opcode[1], Opcode[2], Opcode[3], ~Opcode[4], ~Opcode[5]);  // AND_Gate
  or or_1 (WriteReg, andi_out, RegDst, MemRead, ori_out, addi_out, Link);
  or or_2 (AluSrc, MemRead, MemWrite, andi_out, addi_out, ori_out);
  or or_3 (Branch, beq_out, Bne);
  or or_4 (Jump, j_out, Link);
  or or_5 (AluOp[0], MemRead, MemWrite, Jump, addi_out, ori_out);
  or or_6 (AluOp[1], beq_out, ori_out, Bne);
  or or_7 (AluOp[2], 1'b0, andi_out);

  assign MemToReg = MemRead;

  // Notes on the sheet:
  //   Formato R
  //   lw
  //   sw
  //   beq
  //   addi
  //   bne
  //   j
  //   jal
  //   ori
  //   andi
  //   OPCODE
  //   000000
  //   100011
  //   101011
  //   000100
  //   001000
  //   000101
  //   000010
  //   000011
  //   001101
  //   001100
  //   RegDst
  //   1
  //   0
  //   0
  //   0
  //   0
  //   0
  //   0
  //   1
  //   0
  //   0
  //   0
  //   0
  //   0
  //   1
  //   0
  //   1
  //   0
  //   1
  //   WriteReg
  //   AluSrc
  //   0
  //   1
  //   1
  //   1
  //   1
  //   0
  //   1
  //   0
  //   0
  //   0
  //   1
  //   1
  //   MemRead
  //   0
  //   1
  //   0
  //   0
  //   0
  //   0
  //   0
  //   0
  //   0
  //   0
  //   MemToReg
  //   0
  //   1
  //   0
  //   0
  //   0
  //   0
  //   0
  //   0
  //   0
  //   0
  //   MemWrite
  //   0
  //   0
  //   1
  //   0
  //   0
  //   0
  //   0
  //   0
  //   0
  //   0
  //   Branch
  //   0
  //   0
  //   0
  //   1
  //   0
  //   1
  //   0
  //   0
  //   0
  //   0
  //   Bne
  //   0
  //   0
  //   0
  //   0
  //   0
  //   1
  //   0
  //   0
  //   0
  //   0
  //   Jump
  //   0
  //   0
  //   0
  //   0
  //   0
  //   0
  //   1
  //   1
  //   0
  //   0
  //   AluOp2
  //   Link
  //   0
  //   0
  //   0
  //   0
  //   0
  //   0
  //   0
  //   0
  //   0
  //   0
  //   0
  //   0
  //   1
  //   0
  //   0
  //   0
  //   1
  //   AluOp1
  //   0
  //   0
  //   0
  //   1
  //   0
  //   0
  //   1
  //   0
  //   0
  //   1
  //   0
  //   1
  //   0
  //   AluOp0
  //   0
  //   1
  //   1
  //   0
  //   1
  //   0
  //   0
  //   1
  //   1
  //   0
  //   AluOp
  //   000 - Nada
  //   001 - ADD
  //   010 - SUB
  //   011 - OR
  //   100 - AND
endmodule

module extensor_16bits (
  input  [15:0] in_1,
  output [31:0] out_2
);


  assign out_2 = {{17{in_1[15]}}, in_1[14:0]};
endmodule

module controle_ULA (
  input  [5:0] funct,
  input  [2:0] AluOp,
  output [3:0] Op_ULA,
  output Jr
);

  wire and_1_out;
  wire [2:0] not_6_out;
  wire [3:0] multiplexer_1_out, multiplexer_2_out, multiplexer_3_out, not_3_out, not_11_out, not_14_out,
       not_20_out;
  wire [3:1] not_1_out, not_17_out;
  wire [3:2] not_9_out;
  wire [3:3] not_5_out;

  not not_1 (not_1_out[1], 1'b1);
  not not_2 (not_1_out[3], 1'b1);
  not not_3 (not_3_out[0], 1'b1);
  not not_4 (not_3_out[3], 1'b1);
  not not_5 (not_5_out[3], 1'b1);
  not not_6 (not_6_out[0], 1'b1);
  not not_7 (not_6_out[1], 1'b1);
  not not_8 (not_6_out[2], 1'b1);
  not not_9 (not_9_out[2], 1'b1);
  not not_10 (not_9_out[3], 1'b1);
  not not_11 (not_11_out[0], 1'b1);
  not not_12 (not_11_out[2], 1'b1);
  not not_13 (not_11_out[3], 1'b1);
  not not_14 (not_14_out[0], 1'b1);
  not not_15 (not_14_out[1], 1'b1);
  not not_16 (not_14_out[3], 1'b1);
  not not_17 (not_17_out[1], 1'b1);
  not not_18 (not_17_out[2], 1'b1);
  not not_19 (not_17_out[3], 1'b1);
  not not_20 (not_20_out[0], 1'b1);
  not not_21 (not_20_out[1], 1'b1);
  not not_22 (not_20_out[2], 1'b1);
  not not_23 (not_20_out[3], 1'b1);
  Multiplexer #(.width(4)) multiplexer_1 (
    .in0({not_5_out[3], 3'b111}), .in1({not_1_out[3], 1'b1, not_1_out[1], 1'b1}), .out(multiplexer_1_out),
    .sel(funct[5]));  // open: en
  Multiplexer #(.width(4)) multiplexer_2 (
    .in0({1'b1, not_6_out}), .in1({not_3_out[3], 2'b11, not_3_out[0]}), .out(multiplexer_2_out),
    .sel(funct[5]));  // open: en
  Multiplexer #(.select(4), .width(4)) multiplexer_3 (
    .in0(multiplexer_1_out), .in2(multiplexer_2_out), .in4(not_20_out), .in5({not_17_out, 1'b1}),
    .in6({not_9_out, 2'b11}), .in7({not_11_out[3:2], 1'b1, not_11_out[0]}), .in8(not_20_out),
    .in10({not_14_out[3], 1'b1, not_14_out[1:0]}), .out(multiplexer_3_out), .sel(funct[3:0]));  // open: in1, in3, in9, in11, in12, in13, in14, in15, en
  Multiplexer #(.select(3), .width(4)) multiplexer_4 (
    .in0(multiplexer_3_out), .in1({not_1_out[3], 1'b1, not_1_out[1], 1'b1}),
    .in2({not_3_out[3], 2'b11, not_3_out[0]}), .in3({not_17_out, 1'b1}), .in4(not_20_out), .out(Op_ULA),
    .sel(AluOp));  // open: in5, in6, in7, en
  and and_1 (and_1_out, ~funct[0], ~funct[1], ~funct[2], funct[3]);  // AND_Gate
  and and_2 (Jr, ~AluOp[0], ~AluOp[1], ~AluOp[2], and_1_out);  // AND_Gate

  // Notes on the sheet:
  //   add
  //   sub
  //   or
  //   and
  //   sll
  //   srl
  //   xor
  //   nor
  //   slt
  //   0: sll
  //   1: add
  //   0: srl
  //   1: sub
  //   Funct
  //   000000
  //   000010
  //   000100
  //   000101
  //   000110
  //   000111
  //   001000
  //   001010
  //   Operação
  //   sll
  //   srl
  //   and
  //   or
  //   xor
  //   nor
  //   jr
  //   slt
  //   Op(ULA)
  //   0111
  //   1000
  //   0000
  //   0001
  //   0011
  //   0010
  //   0000
  //   0100
endmodule

module decodificador_instrucoes (
  input  [31:0] \Instrução ,
  output [15:0] imm,
  output [25:0] addr,
  output [4:0] rs,
  output [4:0] rt,
  output [4:0] rd,
  output [4:0] shamt,
  output [5:0] funct,
  output [5:0] opcode
);


  assign addr = \Instrução [25:0];
  assign funct = \Instrução [5:0];
  assign imm = \Instrução [15:0];
  assign opcode = \Instrução [31:26];
  assign rd = \Instrução [15:11];
  assign rs = \Instrução [25:21];
  assign rt = \Instrução [20:16];
  assign shamt = \Instrução [10:6];
endmodule

module _2conc (
  input  [25:0] Addr,
  input  [31:0] Pc_4,
  output [31:0] out_3
);

  wire [27:26] undriven;

  Shifter #(.width(28)) shifter_1 (.in({undriven, {8{1'b0}}, Addr[17:0]}), .\dist (5'b00010), .out(out_3[27:0]));

  assign out_3[31:28] = Pc_4[31:28];
endmodule
